// Logisim project C1.circ as structural Verilog: 2 circuits, main circuit truthtable
module truthtable (
  input  [1:0] in_1,
  input  in_2,
  input  in_3,
  input  in_4,
  input  in_5,
  input  in_6,
  input  in_7,
  input  in_8,
  input  in_9,
  input  in_10,
  input  in_11,
  input  in_12,
  input  in_13,
  input  in_14,
  input  in_15,
  input  in_16,
  input  in_17,
  input  in_18,
  input  in_19,
  input  in_20,
  input  in_21,
  input  in_22,
  input  in_23,
  input  in_24,
  input  in_25,
  input  in_26,
  input  in_27,
  input  in_28,
  input  in_29,
  input  in_30,
  input  in_31,
  input  in_32,
  input  in_33,
  input  in_34,
  output out_35,
  output out_36,
  output out_37,
  output out_38,
  output out_39,
  output out_40,
  output out_41,
  output out_42,
  output out_43,
  output out_44,
  output out_45,
  output out_46,
  output out_47,
  output out_48,
  output out_49,
  output out_50
);

  wire [3:2] undriven;

  Circuit_1 circuit_1_1 (
    .A0(in_3), .B0(in_19), .in_5(in_4), .in_6(in_20), .in_7(in_5), .in_8(in_21), .in_9(in_6), .in_10(in_22),
    .in_11(in_7), .in_12(in_23), .in_13(in_8), .in_14(in_24), .in_15(in_9), .in_16(in_25), .in_17(in_10),
    .in_18(in_26), .in_19(in_11), .in_20(in_27), .in_21(in_12), .in_22(in_28), .in_23(in_13), .in_24(in_29),
    .in_25(in_14), .in_26(in_30), .in_27(in_15), .in_28(in_31), .in_29(in_16), .in_30(in_32), .in_31(in_17),
    .in_32(in_33), .in_33(in_18), .in_34(in_34), .out_35(out_35), .out_36(out_36), .out_37(out_37),
    .out_38(out_38), .out_39(out_39), .out_40(out_40), .out_41(out_41), .out_42(out_42), .out_43(out_43),
    .out_44(out_44), .out_45(out_45), .out_46(out_46), .out_47(out_47), .out_48(out_48), .out_49(out_49),
    .in_1({undriven, in_1}), .in_2(in_2), .out_51(out_50));  // open: Carry, Overflow
  // Pins of 2 and 4 bits meet at {undriven, in_1}

  // Notes on the sheet:
  //   0
  //   0
  //   0
  //   1
  //   1
  //   0
  //   1
  //   1
  //   0
  //   0
  //   0
  //   1
  //   1
  //   0
  //   1
  //   1
  //   S1     S0     C            OPERATION
  //   0
  //   0
  //   0
  //   0
  //   1
  //   1
  //   1
  //   1
  //   TRANSFER A
  //   ADDITION
  //   SUBTRACTION WITH BURROW
  //   DECREMENT
  //   INCREMENT A
  //   ADDITION WITH CARRY
  //   SUBTRACTION
  //   TRANSFER A
endmodule

module Circuit_1 (
  input  [3:0] in_1,
  input  in_2,
  input  A0,
  input  B0,
  input  in_5,
  input  in_6,
  input  in_7,
  input  in_8,
  input  in_9,
  input  in_10,
  input  in_11,
  input  in_12,
  input  in_13,
  input  in_14,
  input  in_15,
  input  in_16,
  input  in_17,
  input  in_18,
  input  in_19,
  input  in_20,
  input  in_21,
  input  in_22,
  input  in_23,
  input  in_24,
  input  in_25,
  input  in_26,
  input  in_27,
  input  in_28,
  input  in_29,
  input  in_30,
  input  in_31,
  input  in_32,
  input  in_33,
  input  in_34,
  output out_35,
  output out_36,
  output out_37,
  output out_38,
  output out_39,
  output out_40,
  output out_41,
  output out_42,
  output out_43,
  output out_44,
  output out_45,
  output out_46,
  output out_47,
  output out_48,
  output out_49,
  output Overflow,
  output out_51,
  output Carry
);

  wire adder_1_cout, adder_2_cout, adder_3_cout, adder_4_cout, adder_5_cout, adder_6_cout, adder_7_cout,
       adder_8_cout, adder_9_cout, adder_10_cout, adder_11_cout, adder_12_cout, adder_13_cout, adder_14_cout,
       adder_15_cout, and_1_out, and_2_out, and_3_out, and_4_out, multiplexer_1_out, multiplexer_2_out,
       multiplexer_3_out, multiplexer_4_out, multiplexer_5_out, multiplexer_6_out, multiplexer_7_out,
       multiplexer_8_out, multiplexer_9_out, multiplexer_10_out, multiplexer_11_out, multiplexer_12_out,
       multiplexer_13_out, multiplexer_14_out, multiplexer_15_out, multiplexer_16_out, not_1_out, not_2_out,
       not_3_out, not_4_out, not_5_out, not_6_out, not_7_out, not_8_out, not_9_out, not_10_out, not_11_out,
       not_12_out, not_13_out, not_14_out, not_15_out, not_16_out, not_17_out, not_18_out, not_19_out,
       not_20_out, not_21_out, not_22_out, or_1_out;

  not not_1 (not_1_out, 1'b0);
  not not_2 (not_2_out, B0);
  not not_3 (not_3_out, in_6);
  not not_4 (not_4_out, in_8);
  not not_5 (not_5_out, in_10);
  not not_6 (not_6_out, in_12);
  not not_7 (not_7_out, in_14);
  not not_8 (not_8_out, in_16);
  not not_9 (not_9_out, in_18);
  not not_10 (not_10_out, in_20);
  not not_11 (not_11_out, in_22);
  not not_12 (not_12_out, in_24);
  not not_13 (not_13_out, in_26);
  not not_14 (not_14_out, in_28);
  not not_15 (not_15_out, in_30);
  not not_16 (not_16_out, in_32);
  not not_17 (not_17_out, in_34);
  not not_18 (not_18_out, in_1[2]);
  and and_1 (and_1_out, in_1[3], not_18_out);
  Multiplexer #(.select(2)) multiplexer_1 (
    .in0(1'b0), .in1(B0), .in2(not_2_out), .in3(not_1_out), .out(multiplexer_1_out), .sel(in_1[1:0]),
    .en(and_1_out));
  Multiplexer #(.select(2)) multiplexer_2 (
    .in0(1'b0), .in1(in_6), .in2(not_3_out), .in3(not_1_out), .out(multiplexer_2_out), .sel(in_1[1:0]),
    .en(and_1_out));
  Multiplexer #(.select(2)) multiplexer_3 (
    .in0(1'b0), .in1(in_8), .in2(not_4_out), .in3(not_1_out), .out(multiplexer_3_out), .sel(in_1[1:0]),
    .en(and_1_out));
  Multiplexer #(.select(2)) multiplexer_4 (
    .in0(1'b0), .in1(in_10), .in2(not_5_out), .in3(not_1_out), .out(multiplexer_4_out), .sel(in_1[1:0]),
    .en(and_1_out));
  Multiplexer #(.select(2)) multiplexer_5 (
    .in0(1'b0), .in1(in_12), .in2(not_6_out), .in3(not_1_out), .out(multiplexer_5_out), .sel(in_1[1:0]),
    .en(and_1_out));
  Multiplexer #(.select(2)) multiplexer_6 (
    .in0(1'b0), .in1(in_14), .in2(not_7_out), .in3(not_1_out), .out(multiplexer_6_out), .sel(in_1[1:0]),
    .en(and_1_out));
  Multiplexer #(.select(2)) multiplexer_7 (
    .in0(1'b0), .in1(in_16), .in2(not_8_out), .in3(not_1_out), .out(multiplexer_7_out), .sel(in_1[1:0]),
    .en(and_1_out));
  Multiplexer #(.select(2)) multiplexer_8 (
    .in0(1'b0), .in1(in_18), .in2(not_9_out), .in3(not_1_out), .out(multiplexer_8_out), .sel(in_1[1:0]),
    .en(and_1_out));
  Multiplexer #(.select(2)) multiplexer_9 (
    .in0(1'b0), .in1(in_20), .in2(not_10_out), .in3(not_1_out), .out(multiplexer_9_out), .sel(in_1[1:0]),
    .en(and_1_out));
  Multiplexer #(.select(2)) multiplexer_10 (
    .in0(1'b0), .in1(in_22), .in2(not_11_out), .in3(not_1_out), .out(multiplexer_10_out), .sel(in_1[1:0]),
    .en(and_1_out));
  Multiplexer #(.select(2)) multiplexer_11 (
    .in0(1'b0), .in1(in_24), .in2(not_12_out), .in3(not_1_out), .out(multiplexer_11_out), .sel(in_1[1:0]),
    .en(and_1_out));
  Multiplexer #(.select(2)) multiplexer_12 (
    .in0(1'b0), .in1(in_26), .in2(not_13_out), .in3(not_1_out), .out(multiplexer_12_out), .sel(in_1[1:0]),
    .en(and_1_out));
  Multiplexer #(.select(2)) multiplexer_13 (
    .in0(1'b0), .in1(in_28), .in2(not_14_out), .in3(not_1_out), .out(multiplexer_13_out), .sel(in_1[1:0]),
    .en(and_1_out));
  Multiplexer #(.select(2)) multiplexer_14 (
    .in0(1'b0), .in1(in_30), .in2(not_15_out), .in3(not_1_out), .out(multiplexer_14_out), .sel(in_1[1:0]),
    .en(and_1_out));
  Multiplexer #(.select(2)) multiplexer_15 (
    .in0(1'b0), .in1(in_32), .in2(not_16_out), .in3(not_1_out), .out(multiplexer_15_out), .sel(in_1[1:0]),
    .en(and_1_out));
  Multiplexer #(.select(2)) multiplexer_16 (
    .in0(1'b0), .in1(in_34), .in2(not_17_out), .in3(not_1_out), .out(multiplexer_16_out), .sel(in_1[1:0]),
    .en(and_1_out));
  Adder #(.width(1)) adder_1 (.a(A0), .b(multiplexer_1_out), .out(out_35), .cin(in_2), .cout(adder_1_cout));
  Adder #(.width(1)) adder_2 (.a(in_5), .b(multiplexer_2_out), .out(out_36), .cin(adder_1_cout), .cout(adder_2_cout));
  Adder #(.width(1)) adder_3 (.a(in_7), .b(multiplexer_3_out), .out(out_37), .cin(adder_2_cout), .cout(adder_3_cout));
  Adder #(.width(1)) adder_4 (.a(in_9), .b(multiplexer_4_out), .out(out_38), .cin(adder_3_cout), .cout(adder_4_cout));
  Adder #(.width(1)) adder_5 (.a(in_11), .b(multiplexer_5_out), .out(out_39), .cin(adder_4_cout), .cout(adder_5_cout));
  Adder #(.width(1)) adder_6 (.a(in_13), .b(multiplexer_6_out), .out(out_40), .cin(adder_5_cout), .cout(adder_6_cout));
  Adder #(.width(1)) adder_7 (.a(in_15), .b(multiplexer_7_out), .out(out_41), .cin(adder_6_cout), .cout(adder_7_cout));
  Adder #(.width(1)) adder_8 (.a(in_17), .b(multiplexer_8_out), .out(out_42), .cin(adder_7_cout), .cout(adder_8_cout));
  Adder #(.width(1)) adder_9 (.a(in_19), .b(multiplexer_9_out), .out(out_43), .cin(adder_8_cout), .cout(adder_9_cout));
  Adder #(.width(1)) adder_10 (
    .a(in_21), .b(multiplexer_10_out), .out(out_44), .cin(adder_9_cout), .cout(adder_10_cout));
  Adder #(.width(1)) adder_11 (
    .a(in_23), .b(multiplexer_11_out), .out(out_45), .cin(adder_10_cout), .cout(adder_11_cout));
  Adder #(.width(1)) adder_12 (
    .a(in_25), .b(multiplexer_12_out), .out(out_46), .cin(adder_11_cout), .cout(adder_12_cout));
  Adder #(.width(1)) adder_13 (
    .a(in_27), .b(multiplexer_13_out), .out(out_47), .cin(adder_12_cout), .cout(adder_13_cout));
  Adder #(.width(1)) adder_14 (
    .a(in_29), .b(multiplexer_14_out), .out(out_48), .cin(adder_13_cout), .cout(adder_14_cout));
  Adder #(.width(1)) adder_15 (
    .a(in_31), .b(multiplexer_15_out), .out(out_49), .cin(adder_14_cout), .cout(adder_15_cout));
  Adder #(.width(1)) adder_16 (.a(in_33), .b(multiplexer_16_out), .out(out_51), .cin(adder_15_cout), .cout(Carry));
  not not_19 (not_19_out, in_33);
  not not_20 (not_20_out, multiplexer_16_out);
  not not_21 (not_21_out, out_51);
  not not_22 (not_22_out, in_1[2]);
  and and_2 (and_2_out, in_1[3], not_22_out);
  and and_3 (and_3_out, not_19_out, not_20_out, out_51);
  and and_4 (and_4_out, in_33, not_21_out, multiplexer_16_out);
  or or_1 (or_1_out, and_3_out, and_4_out);
  and and_5 (Overflow, and_2_out, or_1_out);
endmodule
