// Logisim project C3.circ as structural Verilog: 1 circuit, main circuit Shifter
module Shifter (
  input  A0,
  input  A1,
  input  A2,
  input  A3,
  input  A4,
  input  A5,
  input  A6,
  input  A7,
  input  A8,
  input  A9,
  input  A10,
  input  A11,
  input  A12,
  input  A13,
  input  A14,
  input  A15,
  input  [3:0] in_17,
  input  in_18,
  output A0_2,
  output A1_2,
  output A2_2,
  output A3_2,
  output A4_2,
  output A5_2,
  output A6_2,
  output A7_2,
  output A8_2,
  output A9_2,
  output A10_2,
  output A11_2,
  output A12_2,
  output A13_2,
  output A14_2,
  output A15_2,
  output OVERFLOW
);

  wire and_1_out, and_2_out, decoder_1_out0, decoder_1_out1, decoder_1_out2, decoder_1_out3, decoder_1_out4,
       decoder_1_out5, decoder_1_out6, not_1_out, not_2_out, not_3_out, or_1_out, or_2_out, xor_1_out,
       xor_2_out, xor_3_out, xor_4_out;

  Decoder #(.select(5), .enable("false")) decoder_1 (
    .out0(decoder_1_out0), .out1(decoder_1_out1), .out2(decoder_1_out2), .out3(decoder_1_out3),
    .out4(decoder_1_out4), .out5(decoder_1_out5), .out6(decoder_1_out6), .sel({in_17, in_18}));  // open: out7, out8, out9, out10, out11, out12, out13, out14, out15, out16, out17, out18, out19, out20, out21, out22, out23, out24, out25, out26, out27, out28, out29, out30, out31
  not not_1 (not_1_out, in_17[0]);
  not not_2 (not_2_out, in_18);
  not not_3 (not_3_out, in_17[1]);
  and and_1 (and_1_out, in_18, not_1_out, not_3_out);
  and and_2 (and_2_out, not_2_out, in_17[1]);
  Multiplexer multiplexer_1 (.in0(1'b0), .in1(A1), .out(A0_2), .sel(decoder_1_out0), .en(xor_1_out));
  Multiplexer multiplexer_2 (.in0(A0), .in1(A2), .out(A1_2), .sel(decoder_1_out0), .en(xor_1_out));
  Multiplexer multiplexer_3 (.in0(A1), .in1(A3), .out(A2_2), .sel(decoder_1_out0), .en(xor_1_out));
  Multiplexer multiplexer_4 (.in0(A2), .in1(A4), .out(A3_2), .sel(decoder_1_out0), .en(xor_1_out));
  Multiplexer multiplexer_5 (.in0(A3), .in1(A5), .out(A4_2), .sel(decoder_1_out0), .en(xor_1_out));
  Multiplexer multiplexer_6 (.in0(A4), .in1(A6), .out(A5_2), .sel(decoder_1_out0), .en(xor_1_out));
  Multiplexer multiplexer_7 (.in0(A5), .in1(A7), .out(A6_2), .sel(decoder_1_out0), .en(xor_1_out));
  Multiplexer multiplexer_8 (.in0(A6), .in1(A8), .out(A7_2), .sel(decoder_1_out0), .en(xor_1_out));
  Multiplexer multiplexer_9 (.in0(A7), .in1(A9), .out(A8_2), .sel(decoder_1_out0), .en(xor_1_out));
  Multiplexer multiplexer_10 (.in0(A8), .in1(A10), .out(A9_2), .sel(decoder_1_out0), .en(xor_1_out));
  Multiplexer multiplexer_11 (.in0(A9), .in1(A11), .out(A10_2), .sel(decoder_1_out0), .en(xor_1_out));
  Multiplexer multiplexer_12 (.in0(A10), .in1(A12), .out(A11_2), .sel(decoder_1_out0), .en(xor_1_out));
  Multiplexer multiplexer_13 (.in0(A11), .in1(A13), .out(A12_2), .sel(decoder_1_out0), .en(xor_1_out));
  Multiplexer multiplexer_14 (.in0(A12), .in1(A14), .out(A13_2), .sel(decoder_1_out0), .en(xor_1_out));
  Multiplexer multiplexer_15 (.in0(A13), .in1(A15), .out(A14_2), .sel(decoder_1_out0), .en(xor_1_out));
  Multiplexer multiplexer_16 (.in0(A14), .in1(1'b0), .out(A15_2), .sel(decoder_1_out0), .en(xor_1_out));
  xor xor_1 (xor_1_out, decoder_1_out0, decoder_1_out3);
  or or_1 (or_1_out, and_1_out, and_2_out);
  Multiplexer multiplexer_17 (.in0(A15), .in1(A1), .out(A0_2), .sel(decoder_1_out2), .en(xor_2_out));
  Multiplexer multiplexer_18 (.in0(A0), .in1(A2), .out(A1_2), .sel(decoder_1_out2), .en(xor_2_out));
  Multiplexer multiplexer_19 (.in0(A1), .in1(A3), .out(A2_2), .sel(decoder_1_out2), .en(xor_2_out));
  Multiplexer multiplexer_20 (.in0(A2), .in1(A4), .out(A3_2), .sel(decoder_1_out2), .en(xor_2_out));
  Multiplexer multiplexer_21 (.in0(A3), .in1(A5), .out(A4_2), .sel(decoder_1_out2), .en(xor_2_out));
  Multiplexer multiplexer_22 (.in0(A4), .in1(A6), .out(A5_2), .sel(decoder_1_out2), .en(xor_2_out));
  Multiplexer multiplexer_23 (.in0(A5), .in1(A7), .out(A6_2), .sel(decoder_1_out2), .en(xor_2_out));
  Multiplexer multiplexer_24 (.in0(A6), .in1(A8), .out(A7_2), .sel(decoder_1_out2), .en(xor_2_out));
  Multiplexer multiplexer_25 (.in0(A7), .in1(A9), .out(A8_2), .sel(decoder_1_out2), .en(xor_2_out));
  Multiplexer multiplexer_26 (.in0(A8), .in1(A10), .out(A9_2), .sel(decoder_1_out2), .en(xor_2_out));
  Multiplexer multiplexer_27 (.in0(A9), .in1(A11), .out(A10_2), .sel(decoder_1_out2), .en(xor_2_out));
  Multiplexer multiplexer_28 (.in0(A10), .in1(A12), .out(A11_2), .sel(decoder_1_out2), .en(xor_2_out));
  Multiplexer multiplexer_29 (.in0(A11), .in1(A13), .out(A12_2), .sel(decoder_1_out2), .en(xor_2_out));
  Multiplexer multiplexer_30 (.in0(A12), .in1(A14), .out(A13_2), .sel(decoder_1_out2), .en(xor_2_out));
  Multiplexer multiplexer_31 (.in0(A13), .in1(A15), .out(A14_2), .sel(decoder_1_out2), .en(xor_2_out));
  Multiplexer multiplexer_32 (.in0(A14), .in1(A0), .out(A15_2), .sel(decoder_1_out2), .en(xor_2_out));
  xor xor_2 (xor_2_out, decoder_1_out2, decoder_1_out5);
  or or_2 (or_2_out, decoder_1_out4, decoder_1_out6);
  Multiplexer multiplexer_33 (.in0(1'b0), .in1(A1), .out(A0_2), .sel(decoder_1_out1), .en(xor_3_out));
  Multiplexer multiplexer_34 (.in0(A0), .in1(A2), .out(A1_2), .sel(decoder_1_out1), .en(xor_3_out));
  Multiplexer multiplexer_35 (.in0(A1), .in1(A3), .out(A2_2), .sel(decoder_1_out1), .en(xor_3_out));
  Multiplexer multiplexer_36 (.in0(A2), .in1(A4), .out(A3_2), .sel(decoder_1_out1), .en(xor_3_out));
  Multiplexer multiplexer_37 (.in0(A3), .in1(A5), .out(A4_2), .sel(decoder_1_out1), .en(xor_3_out));
  Multiplexer multiplexer_38 (.in0(A4), .in1(A6), .out(A5_2), .sel(decoder_1_out1), .en(xor_3_out));
  Multiplexer multiplexer_39 (.in0(A5), .in1(A7), .out(A6_2), .sel(decoder_1_out1), .en(xor_3_out));
  Multiplexer multiplexer_40 (.in0(A6), .in1(A8), .out(A7_2), .sel(decoder_1_out1), .en(xor_3_out));
  Multiplexer multiplexer_41 (.in0(A7), .in1(A9), .out(A8_2), .sel(decoder_1_out1), .en(xor_3_out));
  Multiplexer multiplexer_42 (.in0(A8), .in1(A10), .out(A9_2), .sel(decoder_1_out1), .en(xor_3_out));
  Multiplexer multiplexer_43 (.in0(A9), .in1(A11), .out(A10_2), .sel(decoder_1_out1), .en(xor_3_out));
  Multiplexer multiplexer_44 (.in0(A10), .in1(A12), .out(A11_2), .sel(decoder_1_out1), .en(xor_3_out));
  Multiplexer multiplexer_45 (.in0(A11), .in1(A13), .out(A12_2), .sel(decoder_1_out1), .en(xor_3_out));
  Multiplexer multiplexer_46 (.in0(A12), .in1(A14), .out(A13_2), .sel(decoder_1_out1), .en(xor_3_out));
  Multiplexer multiplexer_47 (.in0(A13), .in1(A15), .out(A14_2), .sel(decoder_1_out1), .en(xor_3_out));
  Multiplexer multiplexer_48 (.in0(A14), .in1(A15), .out(A15_2), .sel(decoder_1_out1), .en(xor_3_out));
  xor xor_3 (xor_3_out, decoder_1_out1, or_2_out);
  xor xor_4 (xor_4_out, A15, A14);
  and and_3 (OVERFLOW, or_1_out, xor_4_out);
endmodule
