// Logisim project 1 bit arithmetic unit.circ as structural Verilog: 1 circuit, main circuit arithmetic unit
module arithmetic_unit (
  input  [3:0] S3S2S1S0,
  input  Carry,
  input  A,
  input  B,
  output O,
  output [3:0] S3S2S1S0_2,
  output Carry_2
);

  wire and_1_out, multiplexer_1_out, not_1_out, not_2_out;

  not not_1 (not_1_out, B);
  and and_1 (and_1_out, not_2_out, S3S2S1S0[3]);
  Multiplexer #(.select(2)) multiplexer_1 (
    .in0(1'b0), .in1(B), .in2(not_1_out), .in3(1'b1), .out(multiplexer_1_out), .sel(S3S2S1S0[1:0]),
    .en(and_1_out));
  not not_2 (not_2_out, S3S2S1S0[2]);
  Adder #(.width(1)) adder_1 (.a(A), .b(multiplexer_1_out), .out(O), .cin(Carry), .cout(Carry_2));

  assign S3S2S1S0_2 = S3S2S1S0;
endmodule
