// Logisim project 1 bit logic unit.circ as structural Verilog: 1 circuit, main circuit logic unit
module logic_unit (
  input  Carry,
  input  [3:0] S3S2S1S0,
  input  A,
  input  B,
  output Y,
  output Carry_2,
  output [3:0] S3S2S1S0_2
);

  wire and_1_out, and_2_out, multiplexer_1_out, multiplexer_2_out, multiplexer_3_out, nand_1_out, nor_1_out,
       not_1_out, not_2_out, or_1_out, xnor_1_out, xor_1_out;

  and and_1 (and_1_out, A, B);
  nand nand_1 (nand_1_out, A, B);
  nor nor_1 (nor_1_out, A, B);
  xnor xnor_1 (xnor_1_out, A, B);
  or or_1 (or_1_out, A, B);
  xor xor_1 (xor_1_out, A, B);
  not not_1 (not_1_out, A);
  Multiplexer #(.enable("false")) multiplexer_1 (
    .in0(and_1_out), .in1(nand_1_out), .out(multiplexer_1_out), .sel(Carry));
  Multiplexer #(.enable("false")) multiplexer_2 (
    .in0(nor_1_out), .in1(xnor_1_out), .out(multiplexer_2_out), .sel(Carry));
  Multiplexer #(.enable("false")) multiplexer_3 (.in0(or_1_out), .in1(xor_1_out), .out(multiplexer_3_out), .sel(Carry));
  and and_2 (and_2_out, S3S2S1S0[2], not_2_out);
  Multiplexer #(.select(2)) multiplexer_4 (
    .in0(multiplexer_1_out), .in1(multiplexer_2_out), .in2(multiplexer_3_out), .in3(not_1_out), .out(Y),
    .sel(S3S2S1S0[1:0]), .en(and_2_out));
  not not_2 (not_2_out, S3S2S1S0[3]);

  assign Carry_2 = Carry;
  assign S3S2S1S0_2 = S3S2S1S0;
endmodule
