// Logisim project 1 bit shift unit.circ as structural Verilog: 2 circuits, main circuit 1 bit shift unit
module _1_bit_shift_unit (
  input  Carry,
  input  [3:0] S3S2S1S0,
  input  A0,
  input  A1,
  input  A2,
  input  A3,
  input  A4,
  input  A5,
  output Out,
  output Carry_2,
  output [3:0] S3S2S1S0_2
);

  wire multiplexer_1_out, multiplexer_2_out, multiplexer_3_out, nor_1_out;

  Multiplexer #(.enable("false")) multiplexer_1 (.in0(A0), .in1(A1), .out(multiplexer_1_out), .sel(Carry));
  Multiplexer #(.enable("false")) multiplexer_2 (.in0(A2), .in1(A3), .out(multiplexer_2_out), .sel(Carry));
  Multiplexer #(.enable("false")) multiplexer_3 (.in0(A4), .in1(A5), .out(multiplexer_3_out), .sel(Carry));
  Multiplexer #(.select(2)) multiplexer_4 (
    .in0(multiplexer_1_out), .in1(multiplexer_2_out), .in2(multiplexer_3_out), .out(Out),
    .sel(S3S2S1S0[1:0]), .en(nor_1_out));  // open: in3
  nor nor_1 (nor_1_out, S3S2S1S0[2], S3S2S1S0[3]);

  assign Carry_2 = Carry;
  assign S3S2S1S0_2 = S3S2S1S0;
endmodule

module test (
  input  in_1,
  input  in_2,
  input  in_3,
  input  in_4,
  input  in_5,
  input  in_6,
  input  in_7,
  input  in_8,
  input  in_9,
  input  in_10,
  input  in_11,
  input  in_12,
  input  in_13,
  input  in_14,
  input  in_15,
  input  in_16,
  input  in_17,
  input  [3:0] in_18,
  output out_19,
  output out_20,
  output out_21,
  output out_22,
  output out_23,
  output out_24,
  output out_25,
  output out_26,
  output out_27,
  output out_28,
  output out_29,
  output out_30,
  output out_31,
  output out_32,
  output out_33,
  output out_34
);

  wire n1_bit_shift_unit_1_carry_2, n1_bit_shift_unit_2_carry_2, n1_bit_shift_unit_3_carry_2,
       n1_bit_shift_unit_4_carry_2, n1_bit_shift_unit_5_carry_2, n1_bit_shift_unit_6_carry_2,
       n1_bit_shift_unit_7_carry_2, n1_bit_shift_unit_8_carry_2, n1_bit_shift_unit_9_carry_2,
       n1_bit_shift_unit_10_carry_2, n1_bit_shift_unit_11_carry_2, n1_bit_shift_unit_12_carry_2,
       n1_bit_shift_unit_13_carry_2, n1_bit_shift_unit_14_carry_2, n1_bit_shift_unit_15_carry_2;
  wire [3:0] n1_bit_shift_unit_1_s3s2s1s0_2, n1_bit_shift_unit_2_s3s2s1s0_2, n1_bit_shift_unit_3_s3s2s1s0_2,
       n1_bit_shift_unit_4_s3s2s1s0_2, n1_bit_shift_unit_5_s3s2s1s0_2, n1_bit_shift_unit_6_s3s2s1s0_2,
       n1_bit_shift_unit_7_s3s2s1s0_2, n1_bit_shift_unit_8_s3s2s1s0_2, n1_bit_shift_unit_9_s3s2s1s0_2,
       n1_bit_shift_unit_10_s3s2s1s0_2, n1_bit_shift_unit_11_s3s2s1s0_2, n1_bit_shift_unit_12_s3s2s1s0_2,
       n1_bit_shift_unit_13_s3s2s1s0_2, n1_bit_shift_unit_14_s3s2s1s0_2, n1_bit_shift_unit_15_s3s2s1s0_2;

  _1_bit_shift_unit u_1_bit_shift_unit_1 (
    .Carry(in_1), .S3S2S1S0(in_18), .Carry_2(n1_bit_shift_unit_1_carry_2),
    .S3S2S1S0_2(n1_bit_shift_unit_1_s3s2s1s0_2), .Out(out_19), .A0(in_16), .A2(in_16), .A1(in_16), .A3(1'b0),
    .A4(1'b0), .A5(in_2));
  _1_bit_shift_unit u_1_bit_shift_unit_2 (
    .Carry(n1_bit_shift_unit_1_carry_2), .S3S2S1S0(n1_bit_shift_unit_1_s3s2s1s0_2),
    .Carry_2(n1_bit_shift_unit_2_carry_2), .S3S2S1S0_2(n1_bit_shift_unit_2_s3s2s1s0_2), .Out(out_20),
    .A0(in_15), .A2(in_15), .A1(in_15), .A3(in_17), .A4(in_17), .A5(in_17));
  _1_bit_shift_unit u_1_bit_shift_unit_3 (
    .Carry(n1_bit_shift_unit_2_carry_2), .S3S2S1S0(n1_bit_shift_unit_2_s3s2s1s0_2),
    .Carry_2(n1_bit_shift_unit_3_carry_2), .S3S2S1S0_2(n1_bit_shift_unit_3_s3s2s1s0_2), .Out(out_21),
    .A0(in_14), .A2(in_14), .A1(in_14), .A3(in_16), .A4(in_16), .A5(in_16));
  _1_bit_shift_unit u_1_bit_shift_unit_4 (
    .Carry(n1_bit_shift_unit_3_carry_2), .S3S2S1S0(n1_bit_shift_unit_3_s3s2s1s0_2),
    .Carry_2(n1_bit_shift_unit_4_carry_2), .S3S2S1S0_2(n1_bit_shift_unit_4_s3s2s1s0_2), .Out(out_22),
    .A0(in_13), .A2(in_13), .A1(in_13), .A3(in_15), .A4(in_15), .A5(in_15));
  _1_bit_shift_unit u_1_bit_shift_unit_5 (
    .Carry(n1_bit_shift_unit_4_carry_2), .S3S2S1S0(n1_bit_shift_unit_4_s3s2s1s0_2),
    .Carry_2(n1_bit_shift_unit_5_carry_2), .S3S2S1S0_2(n1_bit_shift_unit_5_s3s2s1s0_2), .Out(out_23),
    .A0(in_12), .A2(in_12), .A1(in_12), .A3(in_14), .A4(in_14), .A5(in_14));
  _1_bit_shift_unit u_1_bit_shift_unit_6 (
    .Carry(n1_bit_shift_unit_5_carry_2), .S3S2S1S0(n1_bit_shift_unit_5_s3s2s1s0_2),
    .Carry_2(n1_bit_shift_unit_6_carry_2), .S3S2S1S0_2(n1_bit_shift_unit_6_s3s2s1s0_2), .Out(out_24),
    .A0(in_11), .A2(in_11), .A1(in_11), .A3(in_13), .A4(in_13), .A5(in_13));
  _1_bit_shift_unit u_1_bit_shift_unit_7 (
    .Carry(n1_bit_shift_unit_6_carry_2), .S3S2S1S0(n1_bit_shift_unit_6_s3s2s1s0_2),
    .Carry_2(n1_bit_shift_unit_7_carry_2), .S3S2S1S0_2(n1_bit_shift_unit_7_s3s2s1s0_2), .Out(out_25),
    .A0(in_10), .A2(in_10), .A1(in_10), .A3(in_12), .A4(in_12), .A5(in_12));
  _1_bit_shift_unit u_1_bit_shift_unit_8 (
    .Carry(n1_bit_shift_unit_7_carry_2), .S3S2S1S0(n1_bit_shift_unit_7_s3s2s1s0_2),
    .Carry_2(n1_bit_shift_unit_8_carry_2), .S3S2S1S0_2(n1_bit_shift_unit_8_s3s2s1s0_2), .Out(out_26),
    .A0(in_9), .A2(in_9), .A1(in_9), .A3(in_11), .A4(in_11), .A5(in_11));
  _1_bit_shift_unit u_1_bit_shift_unit_9 (
    .Carry(n1_bit_shift_unit_8_carry_2), .S3S2S1S0(n1_bit_shift_unit_8_s3s2s1s0_2),
    .Carry_2(n1_bit_shift_unit_9_carry_2), .S3S2S1S0_2(n1_bit_shift_unit_9_s3s2s1s0_2), .Out(out_27),
    .A0(in_8), .A2(in_8), .A1(in_8), .A3(in_10), .A4(in_10), .A5(in_10));
  _1_bit_shift_unit u_1_bit_shift_unit_10 (
    .Carry(n1_bit_shift_unit_9_carry_2), .S3S2S1S0(n1_bit_shift_unit_9_s3s2s1s0_2),
    .Carry_2(n1_bit_shift_unit_10_carry_2), .S3S2S1S0_2(n1_bit_shift_unit_10_s3s2s1s0_2), .Out(out_28),
    .A0(in_7), .A2(in_7), .A1(in_7), .A3(in_9), .A4(in_9), .A5(in_9));
  _1_bit_shift_unit u_1_bit_shift_unit_11 (
    .Carry(n1_bit_shift_unit_10_carry_2), .S3S2S1S0(n1_bit_shift_unit_10_s3s2s1s0_2),
    .Carry_2(n1_bit_shift_unit_11_carry_2), .S3S2S1S0_2(n1_bit_shift_unit_11_s3s2s1s0_2), .Out(out_29),
    .A0(in_6), .A2(in_6), .A1(in_6), .A3(in_8), .A4(in_8), .A5(in_8));
  _1_bit_shift_unit u_1_bit_shift_unit_12 (
    .Carry(n1_bit_shift_unit_11_carry_2), .S3S2S1S0(n1_bit_shift_unit_11_s3s2s1s0_2),
    .Carry_2(n1_bit_shift_unit_12_carry_2), .S3S2S1S0_2(n1_bit_shift_unit_12_s3s2s1s0_2), .Out(out_30),
    .A0(in_5), .A2(in_5), .A1(in_5), .A3(in_7), .A4(in_7), .A5(in_7));
  _1_bit_shift_unit u_1_bit_shift_unit_13 (
    .Carry(n1_bit_shift_unit_12_carry_2), .S3S2S1S0(n1_bit_shift_unit_12_s3s2s1s0_2),
    .Carry_2(n1_bit_shift_unit_13_carry_2), .S3S2S1S0_2(n1_bit_shift_unit_13_s3s2s1s0_2), .Out(out_31),
    .A0(in_4), .A2(in_4), .A1(in_4), .A3(in_6), .A4(in_6), .A5(in_6));
  _1_bit_shift_unit u_1_bit_shift_unit_14 (
    .Carry(n1_bit_shift_unit_13_carry_2), .S3S2S1S0(n1_bit_shift_unit_13_s3s2s1s0_2),
    .Carry_2(n1_bit_shift_unit_14_carry_2), .S3S2S1S0_2(n1_bit_shift_unit_14_s3s2s1s0_2), .Out(out_32),
    .A0(in_3), .A2(in_3), .A1(in_3), .A3(in_5), .A4(in_5), .A5(in_5));
  _1_bit_shift_unit u_1_bit_shift_unit_15 (
    .Carry(n1_bit_shift_unit_14_carry_2), .S3S2S1S0(n1_bit_shift_unit_14_s3s2s1s0_2),
    .Carry_2(n1_bit_shift_unit_15_carry_2), .S3S2S1S0_2(n1_bit_shift_unit_15_s3s2s1s0_2), .Out(out_33),
    .A0(in_2), .A2(in_2), .A1(in_2), .A3(in_4), .A4(in_4), .A5(in_4));
  _1_bit_shift_unit u_1_bit_shift_unit_16 (
    .Carry(n1_bit_shift_unit_15_carry_2), .S3S2S1S0(n1_bit_shift_unit_15_s3s2s1s0_2), .Out(out_34),
    .A0(1'b0), .A2(in_17), .A1(in_2), .A3(in_3), .A4(in_3), .A5(in_3));  // open: Carry_2, S3S2S1S0_2
endmodule
