// Logisim project 16 bit ALU_2.circ as structural Verilog: 3 circuits, main circuit 16 bit ALU
module _16_bit_ALU (
  input  [3:0] S,
  input  [15:0] A,
  input  [15:0] B,
  output [15:0] F
);

  wire arithmetic_unit_1_carry_2, arithmetic_unit_2_carry_2, arithmetic_unit_3_carry_2,
       arithmetic_unit_4_carry_2, arithmetic_unit_5_carry_2, arithmetic_unit_6_carry_2,
       arithmetic_unit_7_carry_2, arithmetic_unit_8_carry_2, arithmetic_unit_9_carry_2,
       arithmetic_unit_10_carry_2, arithmetic_unit_11_carry_2, arithmetic_unit_12_carry_2,
       arithmetic_unit_13_carry_2, arithmetic_unit_14_carry_2, arithmetic_unit_15_carry_2, CCR_out_9,
       CCR_out_10, CCR_out_11, CCR_out_12, CCR_out_13, CCR_out_14, CCR_out_15, CCR_out_16,
       logic_unit_1_carry_2, logic_unit_2_carry_2, logic_unit_3_carry_2, logic_unit_4_carry_2,
       logic_unit_5_carry_2, logic_unit_6_carry_2, logic_unit_7_carry_2, logic_unit_8_carry_2,
       logic_unit_9_carry_2, logic_unit_10_carry_2, logic_unit_11_carry_2, logic_unit_12_carry_2,
       logic_unit_13_carry_2, logic_unit_14_carry_2, logic_unit_15_carry_2, logic_unit_16_carry_2,
       n1_bit_shift_unit_1_carry_2, n1_bit_shift_unit_2_carry_2, n1_bit_shift_unit_3_carry_2,
       n1_bit_shift_unit_4_carry_2, n1_bit_shift_unit_5_carry_2, n1_bit_shift_unit_6_carry_2,
       n1_bit_shift_unit_7_carry_2, n1_bit_shift_unit_8_carry_2, n1_bit_shift_unit_9_carry_2,
       n1_bit_shift_unit_10_carry_2, n1_bit_shift_unit_11_carry_2, n1_bit_shift_unit_12_carry_2,
       n1_bit_shift_unit_13_carry_2, n1_bit_shift_unit_14_carry_2, n1_bit_shift_unit_15_carry_2,
       n1_bit_shift_unit_16_carry_2;
  wire [3:0] arithmetic_unit_1_s3s2s1s0_2, arithmetic_unit_2_s3s2s1s0_2, arithmetic_unit_3_s3s2s1s0_2,
       arithmetic_unit_4_s3s2s1s0_2, arithmetic_unit_5_s3s2s1s0_2, arithmetic_unit_6_s3s2s1s0_2,
       arithmetic_unit_7_s3s2s1s0_2, arithmetic_unit_8_s3s2s1s0_2, arithmetic_unit_9_s3s2s1s0_2,
       arithmetic_unit_10_s3s2s1s0_2, arithmetic_unit_11_s3s2s1s0_2, arithmetic_unit_12_s3s2s1s0_2,
       arithmetic_unit_13_s3s2s1s0_2, arithmetic_unit_14_s3s2s1s0_2, arithmetic_unit_15_s3s2s1s0_2,
       arithmetic_unit_16_carry_2, arithmetic_unit_16_s3s2s1s0_2, logic_unit_1_s3s2s1s0_2,
       logic_unit_2_s3s2s1s0_2, logic_unit_3_s3s2s1s0_2, logic_unit_4_s3s2s1s0_2, logic_unit_5_s3s2s1s0_2,
       logic_unit_6_s3s2s1s0_2, logic_unit_7_s3s2s1s0_2, logic_unit_8_s3s2s1s0_2, logic_unit_9_s3s2s1s0_2,
       logic_unit_10_s3s2s1s0_2, logic_unit_11_s3s2s1s0_2, logic_unit_12_s3s2s1s0_2,
       logic_unit_13_s3s2s1s0_2, logic_unit_14_s3s2s1s0_2, logic_unit_15_s3s2s1s0_2,
       logic_unit_16_s3s2s1s0_2, n1_bit_shift_unit_1_s3s2s1s0_2, n1_bit_shift_unit_2_s3s2s1s0_2,
       n1_bit_shift_unit_3_s3s2s1s0_2, n1_bit_shift_unit_4_s3s2s1s0_2, n1_bit_shift_unit_5_s3s2s1s0_2,
       n1_bit_shift_unit_6_s3s2s1s0_2, n1_bit_shift_unit_7_s3s2s1s0_2, n1_bit_shift_unit_8_s3s2s1s0_2,
       n1_bit_shift_unit_9_s3s2s1s0_2, n1_bit_shift_unit_10_s3s2s1s0_2, n1_bit_shift_unit_11_s3s2s1s0_2,
       n1_bit_shift_unit_12_s3s2s1s0_2, n1_bit_shift_unit_13_s3s2s1s0_2, n1_bit_shift_unit_14_s3s2s1s0_2,
       n1_bit_shift_unit_15_s3s2s1s0_2, n1_bit_shift_unit_16_s3s2s1s0_2;

  Hex_Digit_Display hex_digit_display_1 (.value(A[11:8]));  // open: dp
  Hex_Digit_Display hex_digit_display_2 (.value(A[15:12]));  // open: dp
  Hex_Digit_Display hex_digit_display_3 (.value(A[7:4]));  // open: dp
  Hex_Digit_Display hex_digit_display_4 (.value(A[3:0]));  // open: dp
  Hex_Digit_Display hex_digit_display_5 (.value(B[15:12]));  // open: dp
  Hex_Digit_Display hex_digit_display_6 (.value(B[7:4]));  // open: dp
  Hex_Digit_Display hex_digit_display_7 (.value(B[11:8]));  // open: dp
  Hex_Digit_Display hex_digit_display_8 (.value(B[3:0]));  // open: dp
  logic_unit logic_unit_1 (
    .A(A[0]), .B(B[0]), .Y(F[0]), .Carry(CCR_out_16), .S3S2S1S0(S), .Carry_2(logic_unit_1_carry_2),
    .S3S2S1S0_2(logic_unit_1_s3s2s1s0_2));
  logic_unit logic_unit_2 (
    .A(A[1]), .B(B[1]), .Y(F[1]), .Carry(logic_unit_1_carry_2), .S3S2S1S0(logic_unit_1_s3s2s1s0_2),
    .Carry_2(logic_unit_2_carry_2), .S3S2S1S0_2(logic_unit_2_s3s2s1s0_2));
  logic_unit logic_unit_3 (
    .A(A[2]), .B(B[2]), .Y(F[2]), .Carry(logic_unit_2_carry_2), .S3S2S1S0(logic_unit_2_s3s2s1s0_2),
    .Carry_2(logic_unit_3_carry_2), .S3S2S1S0_2(logic_unit_3_s3s2s1s0_2));
  logic_unit logic_unit_4 (
    .A(A[3]), .B(B[3]), .Y(F[3]), .Carry(logic_unit_3_carry_2), .S3S2S1S0(logic_unit_3_s3s2s1s0_2),
    .Carry_2(logic_unit_4_carry_2), .S3S2S1S0_2(logic_unit_4_s3s2s1s0_2));
  logic_unit logic_unit_5 (
    .A(A[4]), .B(B[4]), .Y(F[4]), .Carry(logic_unit_4_carry_2), .S3S2S1S0(logic_unit_4_s3s2s1s0_2),
    .Carry_2(logic_unit_5_carry_2), .S3S2S1S0_2(logic_unit_5_s3s2s1s0_2));
  logic_unit logic_unit_6 (
    .A(A[5]), .B(B[5]), .Y(F[5]), .Carry(logic_unit_5_carry_2), .S3S2S1S0(logic_unit_5_s3s2s1s0_2),
    .Carry_2(logic_unit_6_carry_2), .S3S2S1S0_2(logic_unit_6_s3s2s1s0_2));
  logic_unit logic_unit_7 (
    .A(A[6]), .B(B[6]), .Y(F[6]), .Carry(logic_unit_6_carry_2), .S3S2S1S0(logic_unit_6_s3s2s1s0_2),
    .Carry_2(logic_unit_7_carry_2), .S3S2S1S0_2(logic_unit_7_s3s2s1s0_2));
  logic_unit logic_unit_8 (
    .A(A[7]), .B(B[7]), .Y(F[7]), .Carry(logic_unit_7_carry_2), .S3S2S1S0(logic_unit_7_s3s2s1s0_2),
    .Carry_2(logic_unit_8_carry_2), .S3S2S1S0_2(logic_unit_8_s3s2s1s0_2));
  logic_unit logic_unit_9 (
    .A(A[8]), .B(B[8]), .Y(F[8]), .Carry(logic_unit_8_carry_2), .S3S2S1S0(logic_unit_8_s3s2s1s0_2),
    .Carry_2(logic_unit_9_carry_2), .S3S2S1S0_2(logic_unit_9_s3s2s1s0_2));
  logic_unit logic_unit_10 (
    .A(A[9]), .B(B[9]), .Y(F[9]), .Carry(logic_unit_9_carry_2), .S3S2S1S0(logic_unit_9_s3s2s1s0_2),
    .Carry_2(logic_unit_10_carry_2), .S3S2S1S0_2(logic_unit_10_s3s2s1s0_2));
  logic_unit logic_unit_11 (
    .A(A[10]), .B(B[10]), .Y(F[10]), .Carry(logic_unit_10_carry_2), .S3S2S1S0(logic_unit_10_s3s2s1s0_2),
    .Carry_2(logic_unit_11_carry_2), .S3S2S1S0_2(logic_unit_11_s3s2s1s0_2));
  logic_unit logic_unit_12 (
    .A(A[11]), .B(B[11]), .Y(F[11]), .Carry(logic_unit_11_carry_2), .S3S2S1S0(logic_unit_11_s3s2s1s0_2),
    .Carry_2(logic_unit_12_carry_2), .S3S2S1S0_2(logic_unit_12_s3s2s1s0_2));
  logic_unit logic_unit_13 (
    .A(A[12]), .B(B[12]), .Y(F[12]), .Carry(logic_unit_12_carry_2), .S3S2S1S0(logic_unit_12_s3s2s1s0_2),
    .Carry_2(logic_unit_13_carry_2), .S3S2S1S0_2(logic_unit_13_s3s2s1s0_2));
  logic_unit logic_unit_14 (
    .A(A[13]), .B(B[13]), .Y(F[13]), .Carry(logic_unit_13_carry_2), .S3S2S1S0(logic_unit_13_s3s2s1s0_2),
    .Carry_2(logic_unit_14_carry_2), .S3S2S1S0_2(logic_unit_14_s3s2s1s0_2));
  logic_unit logic_unit_15 (
    .A(A[14]), .B(B[14]), .Y(F[14]), .Carry(logic_unit_14_carry_2), .S3S2S1S0(logic_unit_14_s3s2s1s0_2),
    .Carry_2(logic_unit_15_carry_2), .S3S2S1S0_2(logic_unit_15_s3s2s1s0_2));
  logic_unit logic_unit_16 (
    .A(A[15]), .B(B[15]), .Y(F[15]), .Carry(logic_unit_15_carry_2), .S3S2S1S0(logic_unit_15_s3s2s1s0_2),
    .Carry_2(logic_unit_16_carry_2), .S3S2S1S0_2(logic_unit_16_s3s2s1s0_2));
  _1_bit_shift_unit u_1_bit_shift_unit_1 (
    .Carry(logic_unit_16_carry_2), .S3S2S1S0(logic_unit_16_s3s2s1s0_2),
    .Carry_2(n1_bit_shift_unit_1_carry_2), .S3S2S1S0_2(n1_bit_shift_unit_1_s3s2s1s0_2), .Out(F[0]),
    .A0(A[1]), .A2(A[1]), .A1(A[1]), .A3(1'b0), .A4(1'b0), .A5(A[15]));
  _1_bit_shift_unit u_1_bit_shift_unit_2 (
    .Carry(n1_bit_shift_unit_1_carry_2), .S3S2S1S0(n1_bit_shift_unit_1_s3s2s1s0_2),
    .Carry_2(n1_bit_shift_unit_2_carry_2), .S3S2S1S0_2(n1_bit_shift_unit_2_s3s2s1s0_2), .Out(F[1]),
    .A0(A[2]), .A2(A[2]), .A1(A[2]), .A3(A[0]), .A4(A[0]), .A5(A[0]));
  _1_bit_shift_unit u_1_bit_shift_unit_3 (
    .Carry(n1_bit_shift_unit_2_carry_2), .S3S2S1S0(n1_bit_shift_unit_2_s3s2s1s0_2),
    .Carry_2(n1_bit_shift_unit_3_carry_2), .S3S2S1S0_2(n1_bit_shift_unit_3_s3s2s1s0_2), .Out(F[2]),
    .A0(A[3]), .A2(A[3]), .A1(A[3]), .A3(A[1]), .A4(A[1]), .A5(A[1]));
  _1_bit_shift_unit u_1_bit_shift_unit_4 (
    .Carry(n1_bit_shift_unit_3_carry_2), .S3S2S1S0(n1_bit_shift_unit_3_s3s2s1s0_2),
    .Carry_2(n1_bit_shift_unit_4_carry_2), .S3S2S1S0_2(n1_bit_shift_unit_4_s3s2s1s0_2), .Out(F[3]),
    .A0(A[4]), .A2(A[4]), .A1(A[4]), .A3(A[2]), .A4(A[2]), .A5(A[2]));
  _1_bit_shift_unit u_1_bit_shift_unit_5 (
    .Carry(n1_bit_shift_unit_4_carry_2), .S3S2S1S0(n1_bit_shift_unit_4_s3s2s1s0_2),
    .Carry_2(n1_bit_shift_unit_5_carry_2), .S3S2S1S0_2(n1_bit_shift_unit_5_s3s2s1s0_2), .Out(F[4]),
    .A0(A[5]), .A2(A[5]), .A1(A[5]), .A3(A[3]), .A4(A[3]), .A5(A[3]));
  _1_bit_shift_unit u_1_bit_shift_unit_6 (
    .Carry(n1_bit_shift_unit_5_carry_2), .S3S2S1S0(n1_bit_shift_unit_5_s3s2s1s0_2),
    .Carry_2(n1_bit_shift_unit_6_carry_2), .S3S2S1S0_2(n1_bit_shift_unit_6_s3s2s1s0_2), .Out(F[5]),
    .A0(A[6]), .A2(A[6]), .A1(A[6]), .A3(A[4]), .A4(A[4]), .A5(A[4]));
  _1_bit_shift_unit u_1_bit_shift_unit_7 (
    .Carry(n1_bit_shift_unit_6_carry_2), .S3S2S1S0(n1_bit_shift_unit_6_s3s2s1s0_2),
    .Carry_2(n1_bit_shift_unit_7_carry_2), .S3S2S1S0_2(n1_bit_shift_unit_7_s3s2s1s0_2), .Out(F[6]),
    .A0(A[7]), .A2(A[7]), .A1(A[7]), .A3(A[5]), .A4(A[5]), .A5(A[5]));
  _1_bit_shift_unit u_1_bit_shift_unit_8 (
    .Carry(n1_bit_shift_unit_7_carry_2), .S3S2S1S0(n1_bit_shift_unit_7_s3s2s1s0_2),
    .Carry_2(n1_bit_shift_unit_8_carry_2), .S3S2S1S0_2(n1_bit_shift_unit_8_s3s2s1s0_2), .Out(F[7]),
    .A0(A[8]), .A2(A[8]), .A1(A[8]), .A3(A[6]), .A4(A[6]), .A5(A[6]));
  _1_bit_shift_unit u_1_bit_shift_unit_9 (
    .Carry(n1_bit_shift_unit_8_carry_2), .S3S2S1S0(n1_bit_shift_unit_8_s3s2s1s0_2),
    .Carry_2(n1_bit_shift_unit_9_carry_2), .S3S2S1S0_2(n1_bit_shift_unit_9_s3s2s1s0_2), .Out(F[8]),
    .A0(A[9]), .A2(A[9]), .A1(A[9]), .A3(A[7]), .A4(A[7]), .A5(A[7]));
  _1_bit_shift_unit u_1_bit_shift_unit_10 (
    .Carry(n1_bit_shift_unit_9_carry_2), .S3S2S1S0(n1_bit_shift_unit_9_s3s2s1s0_2),
    .Carry_2(n1_bit_shift_unit_10_carry_2), .S3S2S1S0_2(n1_bit_shift_unit_10_s3s2s1s0_2), .Out(F[9]),
    .A0(A[10]), .A2(A[10]), .A1(A[10]), .A3(A[8]), .A4(A[8]), .A5(A[8]));
  _1_bit_shift_unit u_1_bit_shift_unit_11 (
    .Carry(n1_bit_shift_unit_10_carry_2), .S3S2S1S0(n1_bit_shift_unit_10_s3s2s1s0_2),
    .Carry_2(n1_bit_shift_unit_11_carry_2), .S3S2S1S0_2(n1_bit_shift_unit_11_s3s2s1s0_2), .Out(F[10]),
    .A0(A[11]), .A2(A[11]), .A1(A[11]), .A3(A[9]), .A4(A[9]), .A5(A[9]));
  _1_bit_shift_unit u_1_bit_shift_unit_12 (
    .Carry(n1_bit_shift_unit_11_carry_2), .S3S2S1S0(n1_bit_shift_unit_11_s3s2s1s0_2),
    .Carry_2(n1_bit_shift_unit_12_carry_2), .S3S2S1S0_2(n1_bit_shift_unit_12_s3s2s1s0_2), .Out(F[11]),
    .A0(A[12]), .A2(A[12]), .A1(A[12]), .A3(A[10]), .A4(A[10]), .A5(A[10]));
  _1_bit_shift_unit u_1_bit_shift_unit_13 (
    .Carry(n1_bit_shift_unit_12_carry_2), .S3S2S1S0(n1_bit_shift_unit_12_s3s2s1s0_2),
    .Carry_2(n1_bit_shift_unit_13_carry_2), .S3S2S1S0_2(n1_bit_shift_unit_13_s3s2s1s0_2), .Out(F[12]),
    .A0(A[13]), .A2(A[13]), .A1(A[13]), .A3(A[11]), .A4(A[11]), .A5(A[11]));
  _1_bit_shift_unit u_1_bit_shift_unit_14 (
    .Carry(n1_bit_shift_unit_13_carry_2), .S3S2S1S0(n1_bit_shift_unit_13_s3s2s1s0_2),
    .Carry_2(n1_bit_shift_unit_14_carry_2), .S3S2S1S0_2(n1_bit_shift_unit_14_s3s2s1s0_2), .Out(F[13]),
    .A0(A[14]), .A2(A[14]), .A1(A[14]), .A3(A[12]), .A4(A[12]), .A5(A[12]));
  _1_bit_shift_unit u_1_bit_shift_unit_15 (
    .Carry(n1_bit_shift_unit_14_carry_2), .S3S2S1S0(n1_bit_shift_unit_14_s3s2s1s0_2),
    .Carry_2(n1_bit_shift_unit_15_carry_2), .S3S2S1S0_2(n1_bit_shift_unit_15_s3s2s1s0_2), .Out(F[14]),
    .A0(A[15]), .A2(A[15]), .A1(A[15]), .A3(A[13]), .A4(A[13]), .A5(A[13]));
  _1_bit_shift_unit u_1_bit_shift_unit_16 (
    .Carry(n1_bit_shift_unit_15_carry_2), .S3S2S1S0(n1_bit_shift_unit_15_s3s2s1s0_2),
    .Carry_2(n1_bit_shift_unit_16_carry_2), .S3S2S1S0_2(n1_bit_shift_unit_16_s3s2s1s0_2), .Out(F[15]),
    .A0(1'b0), .A2(A[0]), .A1(A[15]), .A3(A[14]), .A4(A[14]), .A5(A[14]));
  arithmetic_unit arithmetic_unit_1 (
    .A(A[0]), .B(B[0]), .O(F[0]), .S3S2S1S0(n1_bit_shift_unit_16_s3s2s1s0_2),
    .Carry(n1_bit_shift_unit_16_carry_2), .S3S2S1S0_2(arithmetic_unit_1_s3s2s1s0_2),
    .Carry_2(arithmetic_unit_1_carry_2));
  arithmetic_unit arithmetic_unit_2 (
    .A(A[1]), .B(B[1]), .O(F[1]), .S3S2S1S0(arithmetic_unit_1_s3s2s1s0_2), .Carry(arithmetic_unit_1_carry_2),
    .S3S2S1S0_2(arithmetic_unit_2_s3s2s1s0_2), .Carry_2(arithmetic_unit_2_carry_2));
  arithmetic_unit arithmetic_unit_3 (
    .A(A[2]), .B(B[2]), .O(F[2]), .S3S2S1S0(arithmetic_unit_2_s3s2s1s0_2), .Carry(arithmetic_unit_2_carry_2),
    .S3S2S1S0_2(arithmetic_unit_3_s3s2s1s0_2), .Carry_2(arithmetic_unit_3_carry_2));
  arithmetic_unit arithmetic_unit_4 (
    .A(A[3]), .B(B[3]), .O(F[3]), .S3S2S1S0(arithmetic_unit_3_s3s2s1s0_2), .Carry(arithmetic_unit_3_carry_2),
    .S3S2S1S0_2(arithmetic_unit_4_s3s2s1s0_2), .Carry_2(arithmetic_unit_4_carry_2));
  arithmetic_unit arithmetic_unit_5 (
    .A(A[4]), .B(B[4]), .O(F[4]), .S3S2S1S0(arithmetic_unit_4_s3s2s1s0_2), .Carry(arithmetic_unit_4_carry_2),
    .S3S2S1S0_2(arithmetic_unit_5_s3s2s1s0_2), .Carry_2(arithmetic_unit_5_carry_2));
  arithmetic_unit arithmetic_unit_6 (
    .A(A[5]), .B(B[5]), .O(F[5]), .S3S2S1S0(arithmetic_unit_5_s3s2s1s0_2), .Carry(arithmetic_unit_5_carry_2),
    .S3S2S1S0_2(arithmetic_unit_6_s3s2s1s0_2), .Carry_2(arithmetic_unit_6_carry_2));
  arithmetic_unit arithmetic_unit_7 (
    .A(A[6]), .B(B[6]), .O(F[6]), .S3S2S1S0(arithmetic_unit_6_s3s2s1s0_2), .Carry(arithmetic_unit_6_carry_2),
    .S3S2S1S0_2(arithmetic_unit_7_s3s2s1s0_2), .Carry_2(arithmetic_unit_7_carry_2));
  arithmetic_unit arithmetic_unit_8 (
    .A(A[7]), .B(B[7]), .O(F[7]), .S3S2S1S0(arithmetic_unit_7_s3s2s1s0_2), .Carry(arithmetic_unit_7_carry_2),
    .S3S2S1S0_2(arithmetic_unit_8_s3s2s1s0_2), .Carry_2(arithmetic_unit_8_carry_2));
  arithmetic_unit arithmetic_unit_9 (
    .A(A[8]), .B(B[8]), .O(F[8]), .S3S2S1S0(arithmetic_unit_8_s3s2s1s0_2), .Carry(arithmetic_unit_8_carry_2),
    .S3S2S1S0_2(arithmetic_unit_9_s3s2s1s0_2), .Carry_2(arithmetic_unit_9_carry_2));
  arithmetic_unit arithmetic_unit_10 (
    .A(A[9]), .B(B[9]), .O(F[9]), .S3S2S1S0(arithmetic_unit_9_s3s2s1s0_2), .Carry(arithmetic_unit_9_carry_2),
    .S3S2S1S0_2(arithmetic_unit_10_s3s2s1s0_2), .Carry_2(arithmetic_unit_10_carry_2));
  arithmetic_unit arithmetic_unit_11 (
    .A(A[10]), .B(B[10]), .O(F[10]), .S3S2S1S0(arithmetic_unit_10_s3s2s1s0_2),
    .Carry(arithmetic_unit_10_carry_2), .S3S2S1S0_2(arithmetic_unit_11_s3s2s1s0_2),
    .Carry_2(arithmetic_unit_11_carry_2));
  arithmetic_unit arithmetic_unit_12 (
    .A(A[11]), .B(B[11]), .O(F[11]), .S3S2S1S0(arithmetic_unit_11_s3s2s1s0_2),
    .Carry(arithmetic_unit_11_carry_2), .S3S2S1S0_2(arithmetic_unit_12_s3s2s1s0_2),
    .Carry_2(arithmetic_unit_12_carry_2));
  arithmetic_unit arithmetic_unit_13 (
    .A(A[12]), .B(B[12]), .O(F[12]), .S3S2S1S0(arithmetic_unit_12_s3s2s1s0_2),
    .Carry(arithmetic_unit_12_carry_2), .S3S2S1S0_2(arithmetic_unit_13_s3s2s1s0_2),
    .Carry_2(arithmetic_unit_13_carry_2));
  arithmetic_unit arithmetic_unit_14 (
    .A(A[13]), .B(B[13]), .O(F[13]), .S3S2S1S0(arithmetic_unit_13_s3s2s1s0_2),
    .Carry(arithmetic_unit_13_carry_2), .S3S2S1S0_2(arithmetic_unit_14_s3s2s1s0_2),
    .Carry_2(arithmetic_unit_14_carry_2));
  arithmetic_unit arithmetic_unit_15 (
    .A(A[14]), .B(B[14]), .O(F[14]), .S3S2S1S0(arithmetic_unit_14_s3s2s1s0_2),
    .Carry(arithmetic_unit_14_carry_2), .S3S2S1S0_2(arithmetic_unit_15_s3s2s1s0_2),
    .Carry_2(arithmetic_unit_15_carry_2));
  arithmetic_unit arithmetic_unit_16 (
    .A(A[15]), .B(B[15]), .O(F[15]), .S3S2S1S0(arithmetic_unit_15_s3s2s1s0_2),
    .Carry(arithmetic_unit_15_carry_2), .S3S2S1S0_2(arithmetic_unit_16_s3s2s1s0_2),
    .Carry_2(arithmetic_unit_16_carry_2[0]));
  Overflow_Detection overflow_detection_1 (
    .A14(A[14]), .A15(A[15]), .B15(B[15]), .Out_15(F[15]), .O(arithmetic_unit_16_carry_2[1]),
    .S(arithmetic_unit_16_s3s2s1s0_2), .Carry(n1_bit_shift_unit_16_carry_2));
  Hex_Digit_Display hex_digit_display_9 (.value(F[15:12]));  // open: dp
  Hex_Digit_Display hex_digit_display_10 (.value(F[7:4]));  // open: dp
  Hex_Digit_Display hex_digit_display_11 (.value(F[11:8]));  // open: dp
  Hex_Digit_Display hex_digit_display_12 (.value(F[3:0]));  // open: dp
  // Probe on CCR_out_9
  // Probe on CCR_out_10
  nor Zero (arithmetic_unit_16_carry_2[3], F[0], F[1], F[2], F[3], F[4], F[5], F[6], F[7], F[8], F[9], F[10], F[11], F[12], F[13], F[14], F[15]);
  // Probe on CCR_out_11
  // Probe on CCR_out_14
  // Probe on CCR_out_12
  // Probe on CCR_out_13
  _8_bit_Register CCR (
    .in_1(1'b0), .in_2(1'b0), .in_3(1'b0), .in_4(1'b0), .in_5(arithmetic_unit_16_carry_2[3]), .in_6(F[15]),
    .in_7(arithmetic_unit_16_carry_2[1]), .in_8(arithmetic_unit_16_carry_2[0]), .out_9(CCR_out_9),
    .out_10(CCR_out_10), .out_11(CCR_out_11), .out_12(CCR_out_12), .out_13(CCR_out_13), .out_14(CCR_out_14),
    .out_15(CCR_out_15), .out_16(CCR_out_16));
  // Probe on CCR_out_16
  // Probe on CCR_out_15
endmodule

module _8_bit_Register (
  input  in_1,
  input  in_2,
  input  in_3,
  input  in_4,
  input  in_5,
  input  in_6,
  input  in_7,
  input  in_8,
  output out_9,
  output out_10,
  output out_11,
  output out_12,
  output out_13,
  output out_14,
  output out_15,
  output out_16
);

  wire clock_1_out;

  D_Flip_Flop R (.clk(clock_1_out), .D(in_1), .Q(out_9));  // open: Qn, preset, en, reset
  D_Flip_Flop R_2 (.clk(clock_1_out), .D(in_2), .Q(out_10));  // open: Qn, preset, en, reset
  D_Flip_Flop R_3 (.clk(clock_1_out), .D(in_3), .Q(out_11));  // open: Qn, preset, en, reset
  D_Flip_Flop I (.clk(clock_1_out), .D(in_4), .Q(out_12));  // open: Qn, preset, en, reset
  D_Flip_Flop Z (.clk(clock_1_out), .D(in_5), .Q(out_13));  // open: Qn, preset, en, reset
  D_Flip_Flop N (.clk(clock_1_out), .D(in_6), .Q(out_14));  // open: Qn, preset, en, reset
  D_Flip_Flop O (.clk(clock_1_out), .D(in_7), .Q(out_15));  // open: Qn, preset, en, reset
  Clock clock_1 (.out(clock_1_out));
  D_Flip_Flop C (.clk(clock_1_out), .D(in_8), .Q(out_16));  // open: Qn, preset, en, reset
endmodule

module Overflow_Detection (
  input  Carry,
  input  [3:0] S,
  input  Out_15,
  input  A14,
  input  A15,
  input  B15,
  output O
);

  wire Add_out, and_1_out, and_2_out, and_3_out, Arith_out, not_1_out, not_2_out, not_3_out, not_4_out,
       not_5_out, not_6_out, not_7_out, not_8_out, or_1_out, or_2_out, Subt_out, xor_1_out, xor_2_out,
       xor_3_out;

  not not_1 (not_1_out, S[3]);
  not not_2 (not_2_out, S[0]);
  xor xor_1 (xor_1_out, A15, A14);
  not not_3 (not_3_out, S[2]);
  not not_4 (not_4_out, S[1]);
  not not_5 (not_5_out, S[2]);
  not not_6 (not_6_out, S[0]);
  not not_7 (not_7_out, Carry);
  not not_8 (not_8_out, S[2]);
  and Arith (Arith_out, not_7_out, not_1_out, not_8_out, S[1], not_2_out);
  and Add (Add_out, S[3], not_3_out, not_4_out, S[0]);
  and Subt (Subt_out, S[3], not_5_out, S[1], not_6_out);
  and and_1 (and_1_out, Arith_out, xor_1_out);
  or or_1 (or_1_out, A15, B15);
  or or_2 (or_2_out, B15, Out_15);
  xor xor_2 (xor_2_out, or_1_out, Out_15);
  xor xor_3 (xor_3_out, or_2_out, A15);
  and and_2 (and_2_out, xor_2_out, Add_out);
  and and_3 (and_3_out, xor_3_out, Subt_out);
  or or_3 (O, and_1_out, and_2_out, and_3_out);
endmodule
