// Logisim project ödevson.circ as structural Verilog: 1 circuit, main circuit main
module main (
  input  [3:0] S3_S2_S1_S0,
  input  [15:0] in_2,
  input  [15:0] in_3,
  output [15:0] out_4
);

  wire circuit_1_1_p33, circuit_1_1_p35, circuit_1_1_p36, clock_1_out, d_ff_7_q, logic_unit_1_carry_2,
       logic_unit_2_carry_2, logic_unit_3_carry_2, logic_unit_4_carry_2, logic_unit_5_carry_2,
       logic_unit_6_carry_2, logic_unit_7_carry_2, logic_unit_8_carry_2, logic_unit_9_carry_2,
       logic_unit_10_carry_2, logic_unit_11_carry_2, logic_unit_12_carry_2, logic_unit_13_carry_2,
       logic_unit_14_carry_2, logic_unit_15_carry_2, nor_1_out, or_1_out, shifter_1_overflow, undriven,
       undriven_2, undriven_3, undriven_4;
  wire [3:0] logic_unit_1_s3s2s1s0_2, logic_unit_2_s3s2s1s0_2, logic_unit_3_s3s2s1s0_2,
       logic_unit_4_s3s2s1s0_2, logic_unit_5_s3s2s1s0_2, logic_unit_6_s3s2s1s0_2, logic_unit_7_s3s2s1s0_2,
       logic_unit_8_s3s2s1s0_2, logic_unit_9_s3s2s1s0_2, logic_unit_10_s3s2s1s0_2, logic_unit_11_s3s2s1s0_2,
       logic_unit_12_s3s2s1s0_2, logic_unit_13_s3s2s1s0_2, logic_unit_14_s3s2s1s0_2,
       logic_unit_15_s3s2s1s0_2, logic_unit_16_s3s2s1s0_2;

  Hex_Digit_Display hex_digit_display_1 (.value(in_2[11:8]));  // open: dp
  Hex_Digit_Display hex_digit_display_2 (.value(in_2[15:12]));  // open: dp
  Hex_Digit_Display hex_digit_display_3 (.value(in_2[7:4]));  // open: dp
  Hex_Digit_Display hex_digit_display_4 (.value(in_2[3:0]));  // open: dp
  Hex_Digit_Display hex_digit_display_5 (.value(in_3[15:12]));  // open: dp
  Hex_Digit_Display hex_digit_display_6 (.value(in_3[11:8]));  // open: dp
  Hex_Digit_Display hex_digit_display_7 (.value(in_3[7:4]));  // open: dp
  Hex_Digit_Display hex_digit_display_8 (.value(in_3[3:0]));  // open: dp
  Shifter shifter_1 (
    .A0(in_2[0]), .A1(in_2[1]), .A2(in_2[2]), .A3(in_2[3]), .A4(in_2[4]), .A5(in_2[5]), .A6(in_2[6]),
    .A7(in_2[7]), .A8(in_2[8]), .A9(in_2[9]), .A10(in_2[10]), .A11(in_2[11]), .A12(in_2[12]), .A13(in_2[13]),
    .A14(in_2[14]), .A15(in_2[15]), .A0_2(out_4[0]), .A1_2(out_4[1]), .A2_2(out_4[2]), .A3_2(out_4[3]),
    .A4_2(out_4[4]), .A5_2(out_4[5]), .A6_2(out_4[6]), .A7_2(out_4[7]), .A8_2(out_4[8]), .A9_2(out_4[9]),
    .A10_2(out_4[10]), .A11_2(out_4[11]), .A12_2(out_4[12]), .A13_2(out_4[13]), .A14_2(out_4[14]),
    .A15_2(out_4[15]), .OVERFLOW(shifter_1_overflow), .in_17(logic_unit_16_s3s2s1s0_2),
    .in_18(circuit_1_1_p36));
  // Circuit_1 circuit_1_1: pin names not known; wires that end beside it: in_2[0], in_2[1], in_2[2], in_2[3], in_2[4], in_2[5], in_2[6], in_2[7], in_2[8], in_2[9], in_2[10], in_2[11], in_2[12], in_2[13], in_2[14], in_2[15], in_3[0], in_3[1], in_3[2], in_3[3], in_3[4], in_3[5], in_3[6], in_3[7], in_3[8], in_3[9], in_3[10], in_3[11], in_3[12], in_3[13], in_3[14], in_3[15], circuit_1_1_p33, S3_S2_S1_S0, circuit_1_1_p35, circuit_1_1_p36, out_4[0], out_4[1], out_4[2], out_4[3], out_4[4], out_4[5], out_4[6], out_4[7], out_4[8], out_4[9], out_4[10], out_4[11], out_4[12], out_4[13], out_4[14], out_4[15]
  logic_unit logic_unit_1 (
    .A(in_2[0]), .B(in_3[0]), .Y(out_4[0]), .Carry(d_ff_7_q), .S3S2S1S0(S3_S2_S1_S0),
    .Carry_2(logic_unit_1_carry_2), .S3S2S1S0_2(logic_unit_1_s3s2s1s0_2));
  logic_unit logic_unit_2 (
    .A(in_2[1]), .B(in_3[1]), .Y(out_4[1]), .Carry(logic_unit_1_carry_2), .S3S2S1S0(logic_unit_1_s3s2s1s0_2),
    .Carry_2(logic_unit_2_carry_2), .S3S2S1S0_2(logic_unit_2_s3s2s1s0_2));
  logic_unit logic_unit_3 (
    .A(in_2[2]), .B(in_3[2]), .Y(out_4[2]), .Carry(logic_unit_2_carry_2), .S3S2S1S0(logic_unit_2_s3s2s1s0_2),
    .Carry_2(logic_unit_3_carry_2), .S3S2S1S0_2(logic_unit_3_s3s2s1s0_2));
  logic_unit logic_unit_4 (
    .A(in_2[3]), .B(in_3[3]), .Y(out_4[3]), .Carry(logic_unit_3_carry_2), .S3S2S1S0(logic_unit_3_s3s2s1s0_2),
    .Carry_2(logic_unit_4_carry_2), .S3S2S1S0_2(logic_unit_4_s3s2s1s0_2));
  logic_unit logic_unit_5 (
    .A(in_2[4]), .B(in_3[4]), .Y(out_4[4]), .Carry(logic_unit_4_carry_2), .S3S2S1S0(logic_unit_4_s3s2s1s0_2),
    .Carry_2(logic_unit_5_carry_2), .S3S2S1S0_2(logic_unit_5_s3s2s1s0_2));
  logic_unit logic_unit_6 (
    .A(in_2[5]), .B(in_3[5]), .Y(out_4[5]), .Carry(logic_unit_5_carry_2), .S3S2S1S0(logic_unit_5_s3s2s1s0_2),
    .Carry_2(logic_unit_6_carry_2), .S3S2S1S0_2(logic_unit_6_s3s2s1s0_2));
  logic_unit logic_unit_7 (
    .A(in_2[6]), .B(in_3[6]), .Y(out_4[6]), .Carry(logic_unit_6_carry_2), .S3S2S1S0(logic_unit_6_s3s2s1s0_2),
    .Carry_2(logic_unit_7_carry_2), .S3S2S1S0_2(logic_unit_7_s3s2s1s0_2));
  logic_unit logic_unit_8 (
    .A(in_2[7]), .B(in_3[7]), .Y(out_4[7]), .Carry(logic_unit_7_carry_2), .S3S2S1S0(logic_unit_7_s3s2s1s0_2),
    .Carry_2(logic_unit_8_carry_2), .S3S2S1S0_2(logic_unit_8_s3s2s1s0_2));
  logic_unit logic_unit_9 (
    .A(in_2[8]), .B(in_3[8]), .Y(out_4[8]), .Carry(logic_unit_8_carry_2), .S3S2S1S0(logic_unit_8_s3s2s1s0_2),
    .Carry_2(logic_unit_9_carry_2), .S3S2S1S0_2(logic_unit_9_s3s2s1s0_2));
  logic_unit logic_unit_10 (
    .A(in_2[9]), .B(in_3[9]), .Y(out_4[9]), .Carry(logic_unit_9_carry_2), .S3S2S1S0(logic_unit_9_s3s2s1s0_2),
    .Carry_2(logic_unit_10_carry_2), .S3S2S1S0_2(logic_unit_10_s3s2s1s0_2));
  logic_unit logic_unit_11 (
    .A(in_2[10]), .B(in_3[10]), .Y(out_4[10]), .Carry(logic_unit_10_carry_2),
    .S3S2S1S0(logic_unit_10_s3s2s1s0_2), .Carry_2(logic_unit_11_carry_2),
    .S3S2S1S0_2(logic_unit_11_s3s2s1s0_2));
  logic_unit logic_unit_12 (
    .A(in_2[11]), .B(in_3[11]), .Y(out_4[11]), .Carry(logic_unit_11_carry_2),
    .S3S2S1S0(logic_unit_11_s3s2s1s0_2), .Carry_2(logic_unit_12_carry_2),
    .S3S2S1S0_2(logic_unit_12_s3s2s1s0_2));
  logic_unit logic_unit_13 (
    .A(in_2[12]), .B(in_3[12]), .Y(out_4[12]), .Carry(logic_unit_12_carry_2),
    .S3S2S1S0(logic_unit_12_s3s2s1s0_2), .Carry_2(logic_unit_13_carry_2),
    .S3S2S1S0_2(logic_unit_13_s3s2s1s0_2));
  logic_unit logic_unit_14 (
    .A(in_2[13]), .B(in_3[13]), .Y(out_4[13]), .Carry(logic_unit_13_carry_2),
    .S3S2S1S0(logic_unit_13_s3s2s1s0_2), .Carry_2(logic_unit_14_carry_2),
    .S3S2S1S0_2(logic_unit_14_s3s2s1s0_2));
  logic_unit logic_unit_15 (
    .A(in_2[14]), .B(in_3[14]), .Y(out_4[14]), .Carry(logic_unit_14_carry_2),
    .S3S2S1S0(logic_unit_14_s3s2s1s0_2), .Carry_2(logic_unit_15_carry_2),
    .S3S2S1S0_2(logic_unit_15_s3s2s1s0_2));
  logic_unit logic_unit_16 (
    .A(in_2[15]), .B(in_3[15]), .Y(out_4[15]), .Carry(logic_unit_15_carry_2),
    .S3S2S1S0(logic_unit_15_s3s2s1s0_2), .Carry_2(circuit_1_1_p36), .S3S2S1S0_2(logic_unit_16_s3s2s1s0_2));
  or or_1 (or_1_out, shifter_1_overflow, circuit_1_1_p35);
  D_Flip_Flop d_ff_1 (.clk(clock_1_out), .D(undriven));  // open: Q, Qn, preset, en, reset
  Hex_Digit_Display hex_digit_display_9 (.value(out_4[11:8]));  // open: dp
  Hex_Digit_Display hex_digit_display_10 (.value(out_4[15:12]));  // open: dp
  D_Flip_Flop d_ff_2 (.clk(clock_1_out), .D(undriven_2));  // open: Q, Qn, preset, en, reset
  Hex_Digit_Display hex_digit_display_11 (.value(out_4[3:0]));  // open: dp
  Hex_Digit_Display hex_digit_display_12 (.value(out_4[7:4]));  // open: dp
  D_Flip_Flop d_ff_3 (.clk(clock_1_out), .D(undriven_3));  // open: Q, Qn, preset, en, reset
  nor nor_1 (nor_1_out, out_4[0], out_4[1], out_4[2], out_4[3], out_4[4], out_4[5], out_4[6], out_4[7], out_4[8], out_4[9], out_4[10], out_4[11], out_4[12], out_4[13], out_4[14], out_4[15]);
  D_Flip_Flop d_ff_4 (.clk(clock_1_out), .D(undriven_4));  // open: Q, Qn, preset, en, reset
  D_Flip_Flop d_ff_5 (.clk(clock_1_out), .D(nor_1_out));  // open: Q, Qn, preset, en, reset
  D_Flip_Flop d_ff_6 (.clk(clock_1_out), .D(out_4[15]));  // open: Q, Qn, preset, en, reset
  Clock clock_1 (.out(clock_1_out));
  D_Flip_Flop d_ff_7 (.clk(clock_1_out), .D(circuit_1_1_p33), .Q(d_ff_7_q));  // open: Qn, preset, en, reset
  D_Flip_Flop d_ff_8 (.clk(clock_1_out), .D(or_1_out));  // open: Q, Qn, preset, en, reset

  // Notes on the sheet:
  //   A
  //   B
  //   LOGIC UNIT
  //   ARITMETHIC UNIT
  //   SHIFTER UNIT
  //   CARRY
  //   OUTPUT
  //   R
  //   R
  //   ZERO
  //   R
  //   CCR UNIT
  //   I
  //   ZERO
  //   NEG.
  //   CARRY
  //   CLOCK
  //   OVERFLOW
endmodule
