// Logisim project HW3.circ as structural Verilog: 1 circuit, main circuit main
module main (
);

  wire nor_1_out, nor_2_out, nor_3_out, nor_4_out, nor_5_out, nor_6_out, nor_7_out, nor_8_out, nor_9_out,
       nor_10_out, nor_11_out;

  nor nor_1 (nor_1_out, 1'b1, 1'b1);
  nor nor_2 (nor_2_out, 1'b1, 1'b1);
  nor nor_3 (nor_3_out, 1'b1, 1'b1);
  nor nor_4 (nor_4_out, 1'b1, 1'b1);
  nor nor_5 (nor_5_out, nor_1_out, nor_2_out);
  nor nor_6 (nor_6_out, 1'b1, nor_3_out);
  nor nor_7 (nor_7_out, nor_6_out, 1'b1);
  nor nor_8 (nor_8_out, nor_5_out, nor_7_out);
  nor nor_9 (nor_9_out, nor_8_out, nor_8_out);
  nor nor_10 (nor_10_out, nor_9_out, nor_4_out);
  nor nor_11 (nor_11_out, nor_10_out, nor_10_out);

  // Notes on the sheet:
  //    a 
  //    b 
  //    c 
  //    d 
endmodule
