// Logisim project HW4.circ as structural Verilog: 1 circuit, main circuit main
module main (
  input  in_1,
  input  [3:0] in_2,
  input  in_3,
  input  [3:0] in_4,
  input  in_5,
  input  in_6,
  input  in_7,
  input  A3,
  input  B3,
  input  A2,
  input  B2,
  input  in_12,
  input  A1,
  input  in_14,
  input  in_15,
  input  B1,
  input  in_17,
  input  in_18,
  input  A0,
  input  in_20,
  input  B0,
  input  in_22,
  input  in_23,
  input  in_24,
  input  in_25,
  input  in_26,
  input  in_27,
  input  in_28,
  input  in_29,
  input  in_30,
  input  in_31,
  input  in_32,
  input  A3_2,
  input  in_34,
  input  B3_2,
  input  in_36,
  input  A2_2,
  input  in_38,
  input  in_39,
  input  B2_2,
  input  in_41,
  input  in_42,
  input  A1_2,
  input  in_44,
  input  in_45,
  input  B1_2,
  input  in_47,
  input  in_48,
  input  in_49,
  input  A0_2,
  input  B0_2,
  input  in_52,
  input  in_53,
  input  in_54,
  input  in_55,
  input  in_56,
  input  A3_3,
  input  B3_3,
  input  A2_3,
  input  B2_3,
  input  A1_3,
  input  B1_3,
  input  A0_3,
  input  B0_3,
  output out_65,
  output out_66,
  output Z3,
  output Z2,
  output [4:0] out_69,
  output [3:0] out_70,
  output Z1,
  output Z0,
  output out_73,
  output out_74,
  output out_75,
  output out_76,
  output out_77,
  output out_78,
  output out_79,
  output carry,
  output out_81,
  output out_82,
  output out_83,
  output out_84,
  output out_85,
  output out_86,
  output out_87,
  output out_88,
  output out_89,
  output out_90,
  output out_91,
  output Z3_2,
  output Z2_2,
  output Z1_2,
  output out_95,
  output Z0_2,
  output out_97,
  output out_98,
  output out_99,
  output out_100,
  output out_101,
  output out_102,
  output out_103,
  output out_104,
  output out_105,
  output out_106,
  output out_107,
  output out_108,
  output out_109,
  output carry_2,
  output out_111,
  output out_112,
  output out_113,
  output out_114,
  output Z0_3,
  output Z1_3,
  output Z2_3,
  output Z3_3,
  output out_119,
  output out_120,
  output out_121
);

  wire adder_1_cout, adder_2_cout, adder_3_cout, adder_4_cout, adder_5_cout, adder_6_cout, adder_9_cout,
       adder_10_cout, adder_12_cout, adder_13_cout, adder_14_cout, adder_16_cout, adder_18_cout,
       adder_19_cout, adder_20_cout, adder_21_cout, adder_22_cout, adder_23_cout, adder_24_cout,
       adder_26_cout, and_4_out, not_1_out, not_2_out, not_3_out, not_4_out, not_5_out, not_6_out, not_7_out,
       not_8_out, not_9_out, or_1_out, or_2_out, or_4_out, or_5_out, or_6_out, undriven, xor_1_out,
       xor_2_out, xor_3_out, xor_4_out, xor_5_out, xor_6_out, xor_7_out, xor_8_out, xor_9_out, xor_10_out,
       xor_11_out, xor_12_out, xor_13_out, xor_14_out, xor_15_out, xor_16_out, xor_17_out, xor_18_out,
       xor_19_out, xor_20_out;
  wire [3:0] adder_11_out;

  xor xor_1 (xor_1_out, B3, 1'b1);
  xor xor_2 (xor_2_out, B2, 1'b1);
  xor xor_3 (xor_3_out, B1, 1'b1);
  xor xor_4 (xor_4_out, B0, 1'b1);
  xor xor_5 (xor_5_out, B3_2, in_31);
  xor xor_6 (xor_6_out, B2_2, in_31);
  xor xor_7 (xor_7_out, B1_2, in_31);
  xor xor_8 (xor_8_out, B0_2, in_31);
  xor xor_9 (xor_9_out, A2_3, B2_3);
  xor xor_10 (xor_10_out, A1_3, B1_3);
  Multiplexer #(.enable("false")) multiplexer_1 (.in0(B0), .in1(A0), .out(Z0), .sel(or_4_out));
  Adder #(.width(1)) adder_1 (.a(A3), .b(xor_1_out), .out(out_76), .cin(1'b1), .cout(adder_1_cout));
  Multiplexer #(.enable("false")) multiplexer_2 (.in0(B0_2), .in1(A0_2), .out(Z0_2), .sel(or_6_out));
  Adder #(.width(1)) adder_2 (.a(A3_2), .b(xor_5_out), .out(out_102), .cin(in_31), .cout(adder_2_cout));
  Multiplexer #(.enable("false")) multiplexer_3 (.in0(B0_3), .in1(A0_3), .out(Z3_3), .sel(undriven));
  xor xor_11 (xor_11_out, A3_3, B3_3);
  or or_1 (or_1_out, xor_9_out, B2_3);
  or or_2 (or_2_out, xor_10_out, B1_3);
  Multiplexer #(.enable("false")) multiplexer_4 (.in0(B1), .in1(A1), .out(Z1), .sel(or_5_out));
  Multiplexer #(.enable("false")) multiplexer_5 (.in0(B1_2), .in1(A1_2), .out(Z1_2), .sel(or_6_out));
  Multiplexer #(.enable("false")) multiplexer_6 (.in0(B1_3), .in1(A1_3), .out(Z2_3), .sel(undriven));
  or or_3 (out_119, xor_11_out, B3_3);
  Multiplexer #(.enable("false")) multiplexer_7 (.in0(B2), .in1(A2), .out(Z2), .sel(adder_3_cout));
  Adder #(.width(1)) adder_3 (.a(A2), .b(xor_2_out), .out(out_77), .cin(1'b1), .cout(adder_3_cout));
  Multiplexer #(.enable("false")) multiplexer_8 (.in0(B2_2), .in1(A2_2), .out(Z2_2), .sel(or_6_out));
  Adder #(.width(1)) adder_4 (.a(A2_2), .b(xor_6_out), .out(out_103), .cin(adder_2_cout), .cout(adder_4_cout));
  Multiplexer #(.enable("false")) multiplexer_9 (.in0(B2_3), .in1(A2_3), .out(Z1_3), .sel(undriven));
  and and_1 (out_120, out_119, or_1_out);
  Multiplexer #(.enable("false")) multiplexer_10 (.in0(A3), .in1(B3), .out(Z3), .sel(adder_1_cout));
  Adder #(.width(1)) adder_5 (.a(A1), .b(xor_3_out), .out(out_78), .cin(adder_3_cout), .cout(adder_5_cout));
  and and_2 (Z3_2, B3_2, A3_2);
  Adder #(.width(1)) adder_6 (.a(A1_2), .b(xor_7_out), .out(out_104), .cin(adder_4_cout), .cout(adder_6_cout));
  DotMatrix #(.matrixcols(4), .matrixrows(1)) dotmatrix_1 (.col0(Z0_3), .col1(Z1_3), .col2(Z2_3), .col3(Z3_3));
  and and_3 (Z0_3, B3_3, A3_3);
  DotMatrix #(.matrixcols(4), .matrixrows(1)) dotmatrix_2 (.col0(Z3), .col1(Z2), .col2(Z1), .col3(Z0));
  DotMatrix #(.matrixcols(4), .matrixrows(1)) dotmatrix_3 (.col0(Z3_2), .col1(Z2_2), .col2(Z1_2), .col3(Z0_2));
  and and_4 (and_4_out, out_120, or_2_out);
  or or_4 (or_4_out, or_5_out, carry);
  Adder #(.width(1)) adder_7 (.a(A0), .b(xor_4_out), .out(out_79), .cin(adder_5_cout), .cout(carry));
  Adder #(.width(1)) adder_8 (.a(A0_2), .b(xor_8_out), .out(out_105), .cin(adder_6_cout), .cout(carry_2));
  and and_5 (out_121, out_119, and_4_out);
  or or_5 (or_5_out, adder_3_cout, adder_5_cout);
  xor xor_12 (xor_12_out, adder_6_cout, carry_2);
  or or_6 (or_6_out, xor_12_out, carry_2);
  xor xor_13 (xor_13_out, in_34, 1'b1);
  xor xor_14 (xor_14_out, in_39, 1'b1);
  xor xor_15 (xor_15_out, in_44, 1'b1);
  xor xor_16 (xor_16_out, in_49, 1'b1);
  Adder #(.width(1)) adder_9 (.a(in_32), .b(xor_13_out), .out(out_97), .cin(1'b1), .cout(adder_9_cout));
  not not_1 (not_1_out, in_18);
  not not_2 (not_2_out, in_22);
  not not_3 (not_3_out, in_24);
  not not_4 (not_4_out, in_29);
  Adder #(.width(1)) adder_10 (.a(in_36), .b(xor_14_out), .out(out_98), .cin(adder_9_cout), .cout(adder_10_cout));
  Adder #(.width(4)) adder_11 (.a(in_2), .b(in_4), .out(adder_11_out), .cin(in_1), .cout(out_73));
  Adder #(.width(1)) adder_12 (.a(in_15), .b(not_1_out), .out(out_82), .cin(in_12), .cout(adder_12_cout));
  Adder #(.width(1)) adder_13 (.a(in_42), .b(xor_15_out), .out(out_99), .cin(adder_10_cout), .cout(adder_13_cout));
  assign out_69 = {{1{1'b0}}, adder_11_out};  // Bit_Extender bit_extender_1
  Adder #(.width(1)) adder_14 (.a(in_20), .b(not_2_out), .out(out_83), .cin(adder_12_cout), .cout(adder_14_cout));
  Adder #(.width(1)) adder_15 (.a(in_48), .b(xor_16_out), .out(out_100), .cin(adder_13_cout), .cout(out_111));
  Adder #(.width(1)) adder_16 (.a(in_23), .b(not_3_out), .out(out_84), .cin(adder_14_cout), .cout(adder_16_cout));
  Multiplexer #(.width(4), .enable("false")) multiplexer_11 (.in0(in_2), .in1(in_4), .out(out_70), .sel(out_73));
  Adder #(.width(1)) adder_17 (.a(in_26), .b(not_4_out), .out(out_85), .cin(adder_16_cout), .cout(out_87));
  not not_5 (not_5_out, in_5);
  not not_6 (not_6_out, in_7);
  not not_7 (not_7_out, in_17);
  not not_8 (not_8_out, in_30);
  Adder #(.width(1)) adder_18 (.a(in_3), .b(not_5_out), .out(out_65), .cin(1'b1), .cout(adder_18_cout));
  Adder #(.width(1)) adder_19 (.a(in_6), .b(not_6_out), .out(out_74), .cin(adder_18_cout), .cout(adder_19_cout));
  Adder #(.width(1)) adder_20 (.a(in_14), .b(not_7_out), .out(out_81), .cin(adder_19_cout), .cout(adder_20_cout));
  Adder #(.width(1)) adder_21 (.a(in_28), .b(not_8_out), .out(out_90), .cin(adder_20_cout), .cout(adder_21_cout));
  xor xor_17 (xor_17_out, in_41, 1'b1);
  xor xor_18 (xor_18_out, in_47, 1'b1);
  xor xor_19 (xor_19_out, in_53, 1'b1);
  xor xor_20 (xor_20_out, in_55, 1'b1);
  Multiplexer #(.enable("false")) multiplexer_12 (.in0(in_5), .in1(in_3), .out(out_66), .sel(adder_18_cout));
  Multiplexer #(.enable("false")) multiplexer_13 (.in0(in_7), .in1(in_6), .out(out_75), .sel(adder_19_cout));
  Multiplexer #(.enable("false")) multiplexer_14 (.in0(in_17), .in1(in_14), .out(out_86), .sel(adder_20_cout));
  Multiplexer #(.enable("false")) multiplexer_15 (.in0(in_30), .in1(in_28), .out(out_91), .sel(adder_21_cout));
  Adder #(.width(1)) adder_22 (.a(in_38), .b(xor_17_out), .out(out_106), .cin(1'b1), .cout(adder_22_cout));
  Multiplexer #(.enable("false")) multiplexer_16 (.in0(in_45), .in1(in_47), .out(out_114), .sel(adder_23_cout));
  Multiplexer #(.enable("false")) multiplexer_17 (.in0(in_38), .in1(in_41), .out(out_101), .sel(adder_22_cout));
  Adder #(.width(1)) adder_23 (.a(in_45), .b(xor_18_out), .out(out_107), .cin(adder_22_cout), .cout(adder_23_cout));
  Adder #(.width(1)) adder_24 (.a(in_52), .b(xor_19_out), .out(out_108), .cin(adder_23_cout), .cout(adder_24_cout));
  not not_9 (not_9_out, in_27);
  Multiplexer #(.enable("false")) multiplexer_18 (.in0(in_38), .in1(in_41), .out(out_95), .sel(out_101));
  Adder #(.width(1)) adder_25 (.a(in_54), .b(xor_20_out), .out(out_109), .cin(adder_24_cout), .cout(out_112));
  Adder #(.width(1)) adder_26 (.a(in_25), .b(not_9_out), .out(out_88), .cin(1'b1), .cout(adder_26_cout));
  Multiplexer #(.enable("false")) multiplexer_19 (.in0(in_47), .in1(in_45), .out(out_113), .sel(out_112));
  Multiplexer #(.enable("false")) multiplexer_20 (.in0(in_27), .in1(in_25), .out(out_89), .sel(adder_26_cout));

  // Notes on the sheet:
  //   A>=B  -->  Z=A
  //   A<B  -->  Z=B  
  //   Denemeler
  //   Result
  //   Result
  //   Result
  //   Denemeler
endmodule
