// Logisim project HW5.circ as structural Verilog: 1 circuit, main circuit main
module main (
  input  A,
  input  B,
  input  [1:0] OS,
  input  [1:0] LS,
  output O1,
  output O2,
  output O3
);

  wire decoder_1_out1, decoder_1_out2, decoder_1_out3, multiplexer_1_out, nand_1_out, nand_2_out, nand_3_out,
       nand_4_out, nand_5_out, nand_6_out, nand_7_out, nand_8_out, nand_9_out, nand_10_out, nand_11_out,
       nand_12_out, nand_13_out, nand_14_out, nand_15_out, nand_16_out, nand_17_out, nand_18_out,
       nand_19_out, nand_21_out, nand_23_out, nand_25_out;

  nand nand_1 (nand_1_out, A, A);
  nand nand_2 (nand_2_out, B, B);
  nand nand_3 (nand_3_out, A, A);
  nand nand_4 (nand_4_out, B, B);
  nand nand_5 (nand_5_out, A, A);
  nand nand_6 (nand_6_out, A, B);
  nand nand_7 (nand_7_out, nand_6_out, nand_6_out);
  nand nand_8 (nand_8_out, nand_1_out, nand_2_out);
  nand nand_9 (nand_9_out, nand_3_out, nand_4_out);
  nand nand_10 (nand_10_out, nand_9_out, nand_9_out);
  Multiplexer #(.select(2), .enable("false")) multiplexer_1 (
    .in0(nand_7_out), .in1(nand_8_out), .in2(nand_10_out), .in3(nand_5_out), .out(multiplexer_1_out), .sel(OS));
  Decoder #(.select(2), .enable("false")) decoder_1 (
    .out1(decoder_1_out1), .out2(decoder_1_out2), .out3(decoder_1_out3), .sel(LS));  // open: out0
  nand nand_11 (nand_11_out, multiplexer_1_out, multiplexer_1_out);
  nand nand_12 (nand_12_out, multiplexer_1_out, multiplexer_1_out);
  nand nand_13 (nand_13_out, multiplexer_1_out, multiplexer_1_out);
  nand nand_14 (nand_14_out, multiplexer_1_out, decoder_1_out1);
  nand nand_15 (nand_15_out, decoder_1_out1, nand_11_out);
  nand nand_16 (nand_16_out, multiplexer_1_out, decoder_1_out2);
  nand nand_17 (nand_17_out, decoder_1_out2, nand_12_out);
  nand nand_18 (nand_18_out, multiplexer_1_out, decoder_1_out3);
  nand nand_19 (nand_19_out, decoder_1_out3, nand_13_out);
  nand nand_20 (O1, nand_14_out, nand_21_out);
  nand nand_21 (nand_21_out, O1, nand_15_out);
  nand nand_22 (O2, nand_16_out, nand_23_out);
  nand nand_23 (nand_23_out, O2, nand_17_out);
  nand nand_24 (O3, nand_18_out, nand_25_out);
  nand nand_25 (nand_25_out, O3, nand_19_out);

  // Notes on the sheet:
  //   B
  //   A
endmodule
