// Logisim project 1 bit ALU.circ as structural Verilog: 1 circuit, main circuit main
module main (
  input  in_1,
  input  in_2,
  input  [2:0] in_3,
  input  in_4,
  input  in_5,
  output out_6,
  output out_7,
  output out_8
);

  wire and_1_out, and_2_out, and_3_out, and_4_out, not_1_out, not_2_out, not_3_out, xor_1_out, xor_2_out,
       xor_3_out, xor_4_out, xor_5_out, xor_6_out;

  not not_1 (not_1_out, in_5);
  not not_2 (not_2_out, in_4);
  not not_3 (not_3_out, in_4);
  xor xor_1 (xor_1_out, in_4, in_5);
  and and_1 (and_1_out, in_1, xor_1_out);
  and and_2 (and_2_out, in_4, in_5);
  xor xor_2 (xor_2_out, in_4, not_1_out);
  and and_3 (and_3_out, in_2, xor_2_out);
  and and_4 (and_4_out, in_4, not_1_out);
  xor xor_3 (xor_3_out, not_3_out, 1'b1);
  xor xor_4 (xor_4_out, xor_1_out, in_1);
  or or_1 (out_6, and_1_out, and_2_out);
  xor xor_5 (xor_5_out, xor_2_out, in_2);
  or or_2 (out_7, and_3_out, and_4_out);
  xor xor_6 (xor_6_out, in_4, in_5);
  Multiplexer #(.select(3), .enable("false")) multiplexer_1 (
    .in0(xor_4_out), .in1(xor_5_out), .in2(xor_6_out), .in3(1'b0), .in4(not_2_out), .in5(xor_3_out),
    .in6(in_5), .out(out_8), .sel(in_3));  // open: in7
endmodule
