// Logisim project Camera.circ as structural Verilog
module main (
  input  [1:0] _2_Phase_button
);

  Battery_Test battery_test_1 ();  // open: out_1
  Motor motor_1 ();
  Motor_Cir motor_cir_1 ();  // open: out_6, out_7, in_5, in_4, in_3, out_8, in_1, in_2
  Solenoid_Cir solenoid_cir_1 ();  // open: in_1, in_3, in_2
  _6802 u_6802_1 ();  // open: out_1, out_3, out_5, out_7, out_9, out_11, out_13, out_15, out_17, out_19, out_21, out_23, out_25, out_27, out_29, out_31, out_33, out_35, out_37, out_39, out_2, out_4, out_6, out_8, out_10, out_12, out_14, out_16, out_18, out_20, out_22, out_24, out_26, out_28, out_30, out_32, out_34, out_36, out_38, out_40
  ROM #(.addrWidth(16)) rom_1 ();  // open: addr, data, sel
  Autofocus autofocus_1 ();  // open: in_1, out_6, out_5, in_3, in_2, in_4
  RAM #(.addrWidth(16)) ram_1 ();  // open: addr, data, sel, clk, ld, clr
  _6802 u_6802_2 ();  // open: out_1, out_3, out_5, out_7, out_9, out_11, out_13, out_15, out_17, out_19, out_21, out_23, out_25, out_27, out_29, out_31, out_33, out_35, out_37, out_39, out_2, out_4, out_6, out_8, out_10, out_12, out_14, out_16, out_18, out_20, out_22, out_24, out_26, out_28, out_30, out_32, out_34, out_36, out_38, out_40
  ROM #(.addrWidth(16)) rom_2 ();  // open: addr, data, sel

  // Notes on the sheet:
  //   MOTOR
  //   Main Processor
  //   EEPROM
  //   RAM
  //   Lens Processor
  //   EEPROM
endmodule

module _6802 (
  output out_1,
  output out_2,
  output out_3,
  output out_4,
  output out_5,
  output out_6,
  output out_7,
  output out_8,
  output out_9,
  output out_10,
  output out_11,
  output out_12,
  output out_13,
  output out_14,
  output out_15,
  output out_16,
  output out_17,
  output out_18,
  output out_19,
  output out_20,
  output out_21,
  output out_22,
  output out_23,
  output out_24,
  output out_25,
  output out_26,
  output out_27,
  output out_28,
  output out_29,
  output out_30,
  output out_31,
  output out_32,
  output out_33,
  output out_34,
  output out_35,
  output out_36,
  output out_37,
  output out_38,
  output out_39,
  output out_40
);
endmodule

module Battery_Test (
  output out_1
);
endmodule

module Motor_Cir (
  input  in_1,
  input  in_2,
  input  in_3,
  input  in_4,
  input  in_5,
  output out_6,
  output out_7,
  output out_8
);
endmodule

module Solenoid_Cir (
  input  [7:0] in_1,
  input  in_2,
  input  in_3
);
endmodule

module Autofocus (
  input  in_1,
  input  in_2,
  input  in_3,
  input  in_4,
  output out_5,
  output out_6
);
endmodule
